// Logisim project RISC_V_32.circ as structural Verilog: 12 circuits, main circuit Mikrokontroller
module CPU (
  input  [31:0] juhis,
  input  [31:0] malu_sisend,
  input  reset,
  input  kell,
  input  [31:0] katkestus,
  input  [2:0] malu_viga,
  output [31:0] juhise_aadress,
  output [31:0] ALU_valjund,
  output kirjuta_mallu,
  output [31:0] malu_valjund
);

  wire and_1_out, and_5_out, and_6_out, and_7_out, and_8_out, and_9_out, and_10_out, and_11_out, and_12_out,
       and_13_out, and_14_out, and_15_out, and_16_out, and_17_out, and_18_out, and_19_out, and_20_out,
       and_21_out, buffer_1_out, buffer_2_out, buffer_3_out, comparator_1_eq, comparator_2_eq,
       comparator_3_eq, comparator_4_eq, comparator_5_eq, comparator_6_eq, comparator_7_eq, comparator_8_eq,
       comparator_9_eq, comparator_10_eq, comparator_11_eq, comparator_12_eq, comparator_13_eq,
       juhise_dekodeerija_1_alu_sisend_a, juhise_dekodeerija_1_alu_sisend_b,
       juhise_dekodeerija_1_hargnemise_valik, KasuaadressNihkes, Katkestus_t, kirjutaCSR, MIE_GLOBAL, mret,
       multiplexer_4_out, nor_1_out, not_1_out, not_2_out, not_4_out, or_1_out, or_2_out, or_3_out, or_6_out,
       or_7_out, or_8_out, or_9_out, or_10_out, or_11_out, or_12_out, priority_encoder_1_gs,
       priority_encoder_2_gs, xor_1_out, xor_2_out;
  wire [1:0] juhise_dekodeerija_1_registri_mux;
  wire [2:0] juhise_dekodeerija_1_andmetuup, juhise_dekodeerija_1_erindid, juhise_dekodeerija_1_pc_kontroll;
  wire [3:0] controlled_inverter_1_out, multiplexer_9_out, priority_encoder_1_out, shifter_1_out;
  wire [4:0] controlled_inverter_2_out, juhise_dekodeerija_1_operatsioon, juhise_dekodeerija_1_rd,
       juhise_dekodeerija_1_rsa, juhise_dekodeerija_1_rsb, not_3_out, priority_encoder_2_out;
  wire [11:0] CSRaadress;
  wire [29:0] MEPC_q, MTVEC_q;
  wire [30:0] bit_extender_5_out;
  wire [31:0] adder_1_out, and_2_out, and_3_out, and_4_out, and_22_out, bit_extender_1_out,
       bit_extender_2_out, bit_extender_3_out, bit_extender_4_out, bit_extender_6_out, bit_extender_7_out,
       bit_extender_8_out, bit_extender_9_out, bit_extender_10_out, CSRvaljund, decoder_1_out31,
       juhise_dekodeerija_1_otsene, KatkestuseAadress, KatkestusePohjus, MCYCLE_q, MIE, MIP, MSCRATCH_q,
       mstatus_register_1_andmed_valja, multiplexer_2_out, multiplexer_3_out, multiplexer_5_out,
       multiplexer_6_out, multiplexer_7_out, multiplexer_8_out, multiplexer_10_out, multiplexer_11_out,
       multiplexer_12_out, multiplexer_13_out, multiplexer_14_out, not_5_out, or_13_out,
       registrid_1_register_a, registrid_1_register_b, shifter_2_out, shifter_3_out, TagastusAadress;

  or or_1 (or_1_out, mret, Katkestus_t);
  Multiplexer #(.width(32)) multiplexer_1 (
    .in0(adder_1_out), .in1(ALU_valjund), .out(TagastusAadress), .sel(juhise_dekodeerija_1_pc_kontroll[0]));
  not not_1 (not_1_out, juhise_dekodeerija_1_pc_kontroll[1]);
  Multiplexer #(.width(32)) multiplexer_2 (
    .in0(TagastusAadress), .in1(KatkestuseAadress), .out(multiplexer_2_out), .sel(or_1_out));
  Register #(.width(32)) PC (.D(multiplexer_2_out), .en(or_2_out), .clk(kell), .Q(juhise_aadress), .clr(reset));
  or or_2 (or_2_out, or_1_out, not_1_out);
  Multiplexer #(.width(32)) multiplexer_3 (
    .in0(32'h4), .in1(juhise_dekodeerija_1_otsene), .out(multiplexer_3_out), .sel(and_1_out));
  and and_1 (and_1_out, juhise_dekodeerija_1_pc_kontroll[2], multiplexer_4_out);
  Adder #(.width(32)) adder_1 (.a(multiplexer_3_out), .b(juhise_aadress), .out(adder_1_out));  // open: cin, cout
  Multiplexer multiplexer_4 (
    .in0(or_3_out), .in1(not_2_out), .out(multiplexer_4_out), .sel(juhise_dekodeerija_1_hargnemise_valik));
  not not_2 (not_2_out, or_3_out);
  or or_3 (or_3_out, ALU_valjund[31], ALU_valjund[30], ALU_valjund[29], ALU_valjund[28], ALU_valjund[27], ALU_valjund[26], ALU_valjund[25], ALU_valjund[24], ALU_valjund[23], ALU_valjund[22], ALU_valjund[21], ALU_valjund[20], ALU_valjund[19], ALU_valjund[18], ALU_valjund[17], ALU_valjund[16], ALU_valjund[14], ALU_valjund[13], ALU_valjund[12], ALU_valjund[11], ALU_valjund[10], ALU_valjund[9], ALU_valjund[8], ALU_valjund[7], ALU_valjund[6], ALU_valjund[5], ALU_valjund[4], ALU_valjund[3], ALU_valjund[2], ALU_valjund[1], ALU_valjund[0], ALU_valjund[15]);
  or or_4 (KasuaadressNihkes, juhise_aadress[0], juhise_aadress[1]);
  Decoder #(.enable("false"), .select(5)) decoder_1 (
    .out0(decoder_1_out31[31]), .out1(decoder_1_out31[30]), .out2(decoder_1_out31[29]),
    .out3(decoder_1_out31[28]), .out4(decoder_1_out31[27]), .out5(decoder_1_out31[26]),
    .out6(decoder_1_out31[25]), .out7(decoder_1_out31[24]), .out8(decoder_1_out31[23]),
    .out9(decoder_1_out31[22]), .out10(decoder_1_out31[21]), .out11(decoder_1_out31[20]),
    .out12(decoder_1_out31[19]), .out13(decoder_1_out31[18]), .out14(decoder_1_out31[17]),
    .out15(decoder_1_out31[16]), .out16(decoder_1_out31[15]), .out17(decoder_1_out31[14]),
    .out18(decoder_1_out31[13]), .out19(decoder_1_out31[12]), .out20(decoder_1_out31[11]),
    .out21(decoder_1_out31[10]), .out22(decoder_1_out31[9]), .out23(decoder_1_out31[8]),
    .out24(decoder_1_out31[7]), .out25(decoder_1_out31[6]), .out26(decoder_1_out31[5]),
    .out27(decoder_1_out31[4]), .out28(decoder_1_out31[3]), .out29(decoder_1_out31[2]),
    .out30(decoder_1_out31[1]), .out31(decoder_1_out31[0]), .sel(not_3_out));
  assign not_3_out = ~KatkestusePohjus[4:0];  // NOT_Gate not_3, 5 bits wide
  assign bit_extender_1_out = {{31{KatkestusePohjus[31]}}, KatkestusePohjus[31]};  // Bit_Extender bit_extender_1
  assign bit_extender_2_out = {{31{mret}}, mret};  // Bit_Extender bit_extender_2
  assign and_2_out = bit_extender_1_out & decoder_1_out31;  // AND_Gate and_2, 32 bits wide
  assign and_3_out = and_2_out & bit_extender_2_out;  // AND_Gate and_3, 32 bits wide
  S_R_Flip_Flop #(.trigger("low")) s_r_ff_1 (
    .S(katkestus[0]), .R(and_3_out[0]), .clk(1'b0), .Q(MIP[0]));  // open: reset, Qn, preset
  S_R_Flip_Flop #(.trigger("low")) s_r_ff_2 (
    .S(katkestus[1]), .R(and_3_out[1]), .clk(1'b0), .Q(MIP[1]));  // open: reset, Qn, preset
  S_R_Flip_Flop #(.trigger("low")) s_r_ff_3 (
    .S(katkestus[2]), .R(and_3_out[2]), .clk(1'b0), .Q(MIP[2]));  // open: reset, Qn, preset
  S_R_Flip_Flop #(.trigger("low")) s_r_ff_4 (
    .S(katkestus[3]), .R(and_3_out[3]), .clk(1'b0), .Q(MIP[3]));  // open: reset, Qn, preset
  S_R_Flip_Flop #(.trigger("low")) s_r_ff_5 (
    .S(katkestus[4]), .R(and_3_out[4]), .clk(1'b0), .Q(MIP[4]));  // open: reset, Qn, preset
  S_R_Flip_Flop #(.trigger("low")) s_r_ff_6 (
    .S(katkestus[5]), .R(and_3_out[5]), .clk(1'b0), .Q(MIP[5]));  // open: reset, Qn, preset
  S_R_Flip_Flop #(.trigger("low")) s_r_ff_7 (
    .S(katkestus[6]), .R(and_3_out[6]), .clk(1'b0), .Q(MIP[6]));  // open: reset, Qn, preset
  S_R_Flip_Flop #(.trigger("low")) s_r_ff_8 (
    .S(katkestus[7]), .R(and_3_out[7]), .clk(1'b0), .Q(MIP[7]));  // open: reset, Qn, preset
  S_R_Flip_Flop #(.trigger("low")) s_r_ff_9 (
    .S(katkestus[8]), .R(and_3_out[8]), .clk(1'b0), .Q(MIP[8]));  // open: reset, Qn, preset
  S_R_Flip_Flop #(.trigger("low")) s_r_ff_10 (
    .S(katkestus[9]), .R(and_3_out[9]), .clk(1'b0), .Q(MIP[9]));  // open: reset, Qn, preset
  S_R_Flip_Flop #(.trigger("low")) s_r_ff_11 (
    .S(katkestus[10]), .R(and_3_out[10]), .clk(1'b0), .Q(MIP[10]));  // open: reset, Qn, preset
  S_R_Flip_Flop #(.trigger("low")) s_r_ff_12 (
    .S(katkestus[11]), .R(and_3_out[11]), .clk(1'b0), .Q(MIP[11]));  // open: reset, Qn, preset
  S_R_Flip_Flop #(.trigger("low")) s_r_ff_13 (
    .S(katkestus[12]), .R(and_3_out[12]), .clk(1'b0), .Q(MIP[12]));  // open: reset, Qn, preset
  S_R_Flip_Flop #(.trigger("low")) s_r_ff_14 (
    .S(katkestus[13]), .R(and_3_out[13]), .clk(1'b0), .Q(MIP[13]));  // open: reset, Qn, preset
  S_R_Flip_Flop #(.trigger("low")) s_r_ff_15 (
    .S(katkestus[14]), .R(and_3_out[14]), .clk(1'b0), .Q(MIP[14]));  // open: reset, Qn, preset
  S_R_Flip_Flop #(.trigger("low")) s_r_ff_16 (
    .S(katkestus[15]), .R(and_3_out[15]), .clk(1'b0), .Q(MIP[15]));  // open: reset, Qn, preset
  S_R_Flip_Flop #(.trigger("low")) s_r_ff_17 (
    .S(katkestus[16]), .R(and_3_out[16]), .clk(1'b0), .Q(MIP[16]));  // open: reset, Qn, preset
  S_R_Flip_Flop #(.trigger("low")) s_r_ff_18 (
    .S(katkestus[17]), .R(and_3_out[17]), .clk(1'b0), .Q(MIP[17]));  // open: reset, Qn, preset
  S_R_Flip_Flop #(.trigger("low")) s_r_ff_19 (
    .S(katkestus[18]), .R(and_3_out[18]), .clk(1'b0), .Q(MIP[18]));  // open: reset, Qn, preset
  S_R_Flip_Flop #(.trigger("low")) s_r_ff_20 (
    .S(katkestus[19]), .R(and_3_out[19]), .clk(1'b0), .Q(MIP[19]));  // open: reset, Qn, preset
  S_R_Flip_Flop #(.trigger("low")) s_r_ff_21 (
    .S(katkestus[20]), .R(and_3_out[20]), .clk(1'b0), .Q(MIP[20]));  // open: reset, Qn, preset
  S_R_Flip_Flop #(.trigger("low")) s_r_ff_22 (
    .S(katkestus[21]), .R(and_3_out[21]), .clk(1'b0), .Q(MIP[21]));  // open: reset, Qn, preset
  S_R_Flip_Flop #(.trigger("low")) s_r_ff_23 (
    .S(katkestus[22]), .R(and_3_out[22]), .clk(1'b0), .Q(MIP[22]));  // open: reset, Qn, preset
  S_R_Flip_Flop #(.trigger("low")) s_r_ff_24 (
    .S(katkestus[23]), .R(and_3_out[23]), .clk(1'b0), .Q(MIP[23]));  // open: reset, Qn, preset
  S_R_Flip_Flop #(.trigger("low")) s_r_ff_25 (
    .S(katkestus[24]), .R(and_3_out[24]), .clk(1'b0), .Q(MIP[24]));  // open: reset, Qn, preset
  S_R_Flip_Flop #(.trigger("low")) s_r_ff_26 (
    .S(katkestus[25]), .R(and_3_out[25]), .clk(1'b0), .Q(MIP[25]));  // open: reset, Qn, preset
  S_R_Flip_Flop #(.trigger("low")) s_r_ff_27 (
    .S(katkestus[26]), .R(and_3_out[26]), .clk(1'b0), .Q(MIP[26]));  // open: reset, Qn, preset
  S_R_Flip_Flop #(.trigger("low")) s_r_ff_28 (
    .S(katkestus[27]), .R(and_3_out[27]), .clk(1'b0), .Q(MIP[27]));  // open: reset, Qn, preset
  S_R_Flip_Flop #(.trigger("low")) s_r_ff_29 (
    .S(katkestus[28]), .R(and_3_out[28]), .clk(1'b0), .Q(MIP[28]));  // open: reset, Qn, preset
  S_R_Flip_Flop #(.trigger("low")) s_r_ff_30 (
    .S(katkestus[29]), .R(and_3_out[29]), .clk(1'b0), .Q(MIP[29]));  // open: reset, Qn, preset
  S_R_Flip_Flop #(.trigger("low")) s_r_ff_31 (
    .S(katkestus[30]), .R(and_3_out[30]), .clk(1'b0), .Q(MIP[30]));  // open: reset, Qn, preset
  S_R_Flip_Flop #(.trigger("low")) s_r_ff_32 (
    .S(katkestus[31]), .R(and_3_out[31]), .clk(1'b0), .Q(MIP[31]));  // open: reset, Qn, preset
  Juhise_dekodeerija juhise_dekodeerija_1 (
    .Juhis(juhis), .CSR_aadress(CSRaadress), .mret(mret),
    .Hargnemise_valik(juhise_dekodeerija_1_hargnemise_valik), .PC_kontroll(juhise_dekodeerija_1_pc_kontroll),
    .erindid(juhise_dekodeerija_1_erindid), .Otsene(juhise_dekodeerija_1_otsene),
    .Operatsioon(juhise_dekodeerija_1_operatsioon), .Registri_mux(juhise_dekodeerija_1_registri_mux),
    .ALU_sisend_A(juhise_dekodeerija_1_alu_sisend_a), .rsA(juhise_dekodeerija_1_rsa),
    .rsB(juhise_dekodeerija_1_rsb), .rd(juhise_dekodeerija_1_rd), .andmetuup(juhise_dekodeerija_1_andmetuup),
    .ALU_sisend_B(juhise_dekodeerija_1_alu_sisend_b), .Luba_kirjutamine(kirjuta_mallu),
    .CSR_luba_kirjutamine(kirjutaCSR));
  assign bit_extender_3_out = {{31{MIE_GLOBAL}}, MIE_GLOBAL};  // Bit_Extender bit_extender_3
  assign and_4_out = MIP & bit_extender_3_out & MIE;  // AND_Gate and_4, 32 bits wide
  Priority_Encoder #(.select(4)) priority_encoder_1 (
    .in7(juhise_dekodeerija_1_erindid[1]), .in8(malu_viga[0]), .in9(and_11_out), .in10(malu_viga[1]),
    .in11(and_5_out), .in12(juhise_dekodeerija_1_erindid[2]), .in13(juhise_dekodeerija_1_erindid[0]),
    .in14(malu_viga[2]), .in15(KasuaadressNihkes), .out(priority_encoder_1_out), .gs(priority_encoder_1_gs));  // open: in0, in1, in2, in3, in4, in5, in6, en_out, en_in
  Priority_Encoder #(.select(5)) priority_encoder_2 (
    .in0(and_4_out[31]), .in1(and_4_out[30]), .in2(and_4_out[29]), .in3(and_4_out[28]), .in4(and_4_out[27]),
    .in5(and_4_out[26]), .in6(and_4_out[25]), .in7(and_4_out[24]), .in8(and_4_out[23]), .in9(and_4_out[22]),
    .in10(and_4_out[21]), .in11(and_4_out[20]), .in12(and_4_out[19]), .in13(and_4_out[18]),
    .in14(and_4_out[17]), .in15(and_4_out[16]), .in16(and_4_out[15]), .in17(and_4_out[14]),
    .in18(and_4_out[13]), .in19(and_4_out[12]), .in20(and_4_out[11]), .in21(and_4_out[10]),
    .in22(and_4_out[9]), .in23(and_4_out[8]), .in24(and_4_out[7]), .in25(and_4_out[6]), .in26(and_4_out[5]),
    .in27(and_4_out[4]), .in28(and_4_out[3]), .in29(and_4_out[2]), .in30(and_4_out[1]), .in31(and_4_out[0]),
    .out(priority_encoder_2_out), .gs(priority_encoder_2_gs));  // open: en_out, en_in
  assign bit_extender_4_out = {{28{1'b0}}, controlled_inverter_1_out};  // Bit_Extender bit_extender_4
  assign controlled_inverter_1_out = priority_encoder_1_gs ? ~priority_encoder_1_out : 4'bz;  // Controlled_Inverter controlled_inverter_1
  or or_5 (Katkestus_t, priority_encoder_1_gs, priority_encoder_2_gs);
  assign bit_extender_5_out = {{26{1'b0}}, controlled_inverter_2_out};  // Bit_Extender bit_extender_5
  assign controlled_inverter_2_out = priority_encoder_2_gs ? ~priority_encoder_2_out : 5'bz;  // Controlled_Inverter controlled_inverter_2
  Registrid registrid_1 (
    .Aadress_B(juhise_dekodeerija_1_rsb), .Aadress_A(juhise_dekodeerija_1_rsa),
    .Andmed_sisse(multiplexer_13_out), .Write_address(juhise_dekodeerija_1_rd), .Kell(kell),
    .Register_B(registrid_1_register_b), .Register_A(registrid_1_register_a));  // open: Reset
  assign bit_extender_6_out = {{1{1'b1}}, bit_extender_5_out};  // Bit_Extender bit_extender_6
  and and_5 (and_5_out, and_6_out, or_6_out);
  not not_4 (not_4_out, priority_encoder_1_gs);
  Multiplexer #(.width(32)) multiplexer_5 (
    .in0(bit_extender_4_out), .in1(bit_extender_6_out), .out(multiplexer_5_out), .sel(not_4_out));
  // Probe on registrid_1_register_a
  and and_6 (and_6_out, juhise_dekodeerija_1_registri_mux[1], juhise_dekodeerija_1_registri_mux[0]);
  Multiplexer #(.width(32)) multiplexer_6 (
    .in0(juhise_aadress), .in1(registrid_1_register_a), .out(multiplexer_6_out),
    .sel(juhise_dekodeerija_1_alu_sisend_a));
  Multiplexer #(.width(32)) multiplexer_7 (
    .in0(registrid_1_register_b), .in1(juhise_dekodeerija_1_otsene), .out(multiplexer_7_out),
    .sel(juhise_dekodeerija_1_alu_sisend_b));
  or or_6 (or_6_out, and_9_out, and_10_out);
  and and_7 (and_7_out, ~juhise_dekodeerija_1_andmetuup[2], juhise_dekodeerija_1_andmetuup[1], ~juhise_dekodeerija_1_andmetuup[0]);  // AND_Gate
  and and_8 (and_8_out, ~juhise_dekodeerija_1_andmetuup[2], ~juhise_dekodeerija_1_andmetuup[1], juhise_dekodeerija_1_andmetuup[0]);  // AND_Gate
  or or_7 (or_7_out, and_7_out, and_8_out);
  and and_9 (and_9_out, or_7_out, ALU_valjund[0]);
  ALU_RV32IM ALU (
    .A(multiplexer_6_out), .B(multiplexer_7_out), .Operatsioon(juhise_dekodeerija_1_operatsioon),
    .Tulemus(ALU_valjund));
  nor nor_1 (nor_1_out, juhise_dekodeerija_1_andmetuup[2], juhise_dekodeerija_1_andmetuup[1], juhise_dekodeerija_1_andmetuup[0]);
  and and_10 (and_10_out, nor_1_out, or_8_out);
  and and_11 (and_11_out, kirjuta_mallu, or_9_out);
  // Probe on CSRaadress
  and and_12 (and_12_out, juhise_dekodeerija_1_andmetuup[2], juhise_dekodeerija_1_andmetuup[1], ~juhise_dekodeerija_1_andmetuup[0]);  // AND_Gate
  and and_13 (and_13_out, and_12_out, ALU_valjund[0]);
  Comparator #(.mode("unsigned"), .width(12)) comparator_1 (
    .a(CSRaadress), .b(12'h300), .eq(comparator_1_eq));  // open: gt, lt
  Comparator #(.mode("unsigned"), .width(12)) comparator_2 (
    .a(CSRaadress), .b(12'h301), .eq(comparator_2_eq));  // open: gt, lt
  Comparator #(.mode("unsigned"), .width(12)) comparator_3 (
    .a(CSRaadress), .b(12'h304), .eq(comparator_3_eq));  // open: gt, lt
  Comparator #(.mode("unsigned"), .width(12)) comparator_4 (
    .a(CSRaadress), .b(12'h305), .eq(comparator_4_eq));  // open: gt, lt
  Comparator #(.mode("unsigned"), .width(12)) comparator_5 (
    .a(CSRaadress), .b(12'h341), .eq(comparator_5_eq));  // open: gt, lt
  Comparator #(.mode("unsigned"), .width(12)) comparator_6 (
    .a(CSRaadress), .b(12'h342), .eq(comparator_6_eq));  // open: gt, lt
  Comparator #(.mode("unsigned"), .width(12)) comparator_7 (
    .a(CSRaadress), .b(12'h344), .eq(comparator_7_eq));  // open: gt, lt
  Comparator #(.mode("unsigned"), .width(12)) comparator_8 (
    .a(CSRaadress), .b(12'hb00), .eq(comparator_8_eq));  // open: gt, lt
  Comparator #(.mode("unsigned"), .width(12)) comparator_9 (
    .a(CSRaadress), .b(12'hf00), .eq(comparator_9_eq));  // open: gt, lt
  Comparator #(.mode("unsigned"), .width(12)) comparator_10 (
    .a(CSRaadress), .b(12'hf11), .eq(comparator_10_eq));  // open: gt, lt
  Comparator #(.mode("unsigned"), .width(12)) comparator_11 (
    .a(CSRaadress), .b(12'hf12), .eq(comparator_11_eq));  // open: gt, lt
  Comparator #(.mode("unsigned"), .width(12)) comparator_12 (
    .a(CSRaadress), .b(12'hf13), .eq(comparator_12_eq));  // open: gt, lt
  Comparator #(.mode("unsigned"), .width(12)) comparator_13 (
    .a(CSRaadress), .b(12'hf14), .eq(comparator_13_eq));  // open: gt, lt
  and and_14 (and_14_out, juhise_dekodeerija_1_andmetuup[2], ~juhise_dekodeerija_1_andmetuup[1], juhise_dekodeerija_1_andmetuup[0]);  // AND_Gate
  or or_8 (or_8_out, ALU_valjund[0], ALU_valjund[1]);
  and and_15 (and_15_out, and_14_out, or_8_out);
  or or_9 (or_9_out, and_13_out, and_15_out);
  and and_16 (and_16_out, comparator_1_eq, kirjutaCSR);
  and and_17 (and_17_out, comparator_3_eq, kirjutaCSR);
  buf buffer_1 (buffer_1_out, reset);
  buf buffer_2 (buffer_2_out, reset);
  and and_18 (and_18_out, comparator_5_eq, kirjutaCSR);
  and and_19 (and_19_out, comparator_6_eq, kirjutaCSR);
  and and_20 (and_20_out, comparator_9_eq, kirjutaCSR);
  Multiplexer #(.select(3), .width(32)) multiplexer_8 (
    .in5(registrid_1_register_b), .in6({{16{1'b0}}, registrid_1_register_b[15:0]}),
    .in7({{24{1'b0}}, registrid_1_register_b[7:0]}), .out(multiplexer_8_out),
    .sel(juhise_dekodeerija_1_andmetuup));  // open: in0, in1, in2, in3, in4
  Multiplexer #(.select(3), .width(4)) multiplexer_9 (
    .in5(4'b1111), .in6(4'b0011), .in7(4'b0001), .out(multiplexer_9_out), .sel(juhise_dekodeerija_1_andmetuup));  // open: in0, in1, in2, in3, in4
  Multiplexer #(.width(32)) multiplexer_10 (.in0(ALU_valjund), .in1(32'h4), .out(multiplexer_10_out), .sel(reset));
  and and_21 (and_21_out, comparator_4_eq, kirjutaCSR);
  xor xor_1 (xor_1_out, buffer_1_out, buffer_3_out);
  buf buffer_3 (buffer_3_out, buffer_2_out);
  Multiplexer #(.width(32)) multiplexer_11 (
    .in0(ALU_valjund), .in1(TagastusAadress), .out(multiplexer_11_out), .sel(Katkestus_t));
  Multiplexer #(.width(32)) multiplexer_12 (
    .in0(ALU_valjund), .in1(multiplexer_5_out), .out(multiplexer_12_out), .sel(Katkestus_t));
  Shifter #(.width(4)) shifter_1 (.in(multiplexer_9_out), .\dist (ALU_valjund[1:0]), .out(shifter_1_out));
  Register #(.width(32)) u_MIE (.D(ALU_valjund), .en(and_17_out), .clk(kell), .Q(MIE), .clr(reset));
  Register #(.width(30)) MTVEC (
    .D(multiplexer_10_out[31:2]), .en(or_10_out), .clk(xor_2_out), .Q(MTVEC_q));  // open: clr
  or or_10 (or_10_out, and_21_out, reset);
  xor xor_2 (xor_2_out, kell, xor_1_out);
  Register #(.width(30)) MEPC (.D(multiplexer_11_out[31:2]), .en(or_11_out), .clk(kell), .Q(MEPC_q), .clr(reset));
  or or_11 (or_11_out, Katkestus_t, and_18_out);
  Register #(.width(32)) MCAUSE (.D(multiplexer_12_out), .en(or_12_out), .clk(kell), .Q(KatkestusePohjus), .clr(reset));
  or or_12 (or_12_out, Katkestus_t, and_19_out);
  Register #(.width(32)) MSCRATCH (.D(ALU_valjund), .en(and_20_out), .clk(kell), .Q(MSCRATCH_q), .clr(reset));
  Shifter #(.width(32)) shifter_2 (.in(multiplexer_8_out), .\dist ({ALU_valjund[1:0], 3'b000}), .out(shifter_2_out));
  assign not_5_out = ~{{8{shifter_1_out[3]}}, {8{shifter_1_out[2]}}, {8{shifter_1_out[1]}}, {8{shifter_1_out[0]}}};  // NOT_Gate not_5, 32 bits wide
  assign and_22_out = malu_sisend & not_5_out;  // AND_Gate and_22, 32 bits wide
  Mstatus_register mstatus_register_1 (
    .Andmed_sisse(ALU_valjund), .Luba_kirjutamine(and_16_out), .Loksu_sisenemine(Katkestus_t),
    .Loksust_valjumine(mret), .Reset(reset), .Kell(kell), .Andmed_valja(mstatus_register_1_andmed_valja),
    .mie(MIE_GLOBAL));
  Counter #(.max('hffffffff), .width(32)) MCYCLE (
    .count(1'b1), .Q(MCYCLE_q), .up(1'b1), .clk(kell));  // open: load, D, carry, clr
  assign or_13_out = shifter_2_out | and_22_out;  // OR_Gate or_13, 32 bits wide
  assign malu_valjund = kirjuta_mallu ? or_13_out : 32'bz;  // Controlled_Buffer controlled_buffer_1
  assign CSRvaljund = comparator_1_eq ? mstatus_register_1_andmed_valja : 32'bz;  // Controlled_Buffer controlled_buffer_2
  assign CSRvaljund = comparator_2_eq ? 32'h80000100 : 32'bz;  // Controlled_Buffer controlled_buffer_3
  assign CSRvaljund = comparator_3_eq ? MIE : 32'bz;  // Controlled_Buffer controlled_buffer_4
  assign CSRvaljund = comparator_4_eq ? {MTVEC_q, 2'b00} : 32'bz;  // Controlled_Buffer controlled_buffer_5
  assign KatkestuseAadress = Katkestus_t ? {MTVEC_q, 2'b00} : 32'bz;  // Controlled_Buffer controlled_buffer_6
  assign CSRvaljund = comparator_5_eq ? {MEPC_q, 2'b00} : 32'bz;  // Controlled_Buffer controlled_buffer_7
  assign KatkestuseAadress = mret ? {MEPC_q, 2'b00} : 32'bz;  // Controlled_Buffer controlled_buffer_8
  assign CSRvaljund = comparator_6_eq ? KatkestusePohjus : 32'bz;  // Controlled_Buffer controlled_buffer_9
  assign CSRvaljund = comparator_7_eq ? MIP : 32'bz;  // Controlled_Buffer controlled_buffer_10
  assign CSRvaljund = comparator_8_eq ? MCYCLE_q : 32'bz;  // Controlled_Buffer controlled_buffer_11
  assign CSRvaljund = comparator_9_eq ? MSCRATCH_q : 32'bz;  // Controlled_Buffer controlled_buffer_12
  assign CSRvaljund = comparator_10_eq ? {32{1'b0}} : 32'bz;  // Controlled_Buffer controlled_buffer_13
  assign CSRvaljund = comparator_11_eq ? {32{1'b0}} : 32'bz;  // Controlled_Buffer controlled_buffer_14
  assign CSRvaljund = comparator_12_eq ? {32{1'b0}} : 32'bz;  // Controlled_Buffer controlled_buffer_15
  assign CSRvaljund = comparator_13_eq ? {32{1'b0}} : 32'bz;  // Controlled_Buffer controlled_buffer_16
  Shifter #(.shift("lr"), .width(32)) shifter_3 (
    .in(malu_sisend), .\dist ({ALU_valjund[1:0], 3'b000}), .out(shifter_3_out));
  assign bit_extender_7_out = {{16{shifter_3_out[15]}}, shifter_3_out[15:0]};  // Bit_Extender bit_extender_7
  assign bit_extender_8_out = {{16{1'b0}}, shifter_3_out[15:0]};  // Bit_Extender bit_extender_8
  assign bit_extender_9_out = {{24{shifter_3_out[7]}}, shifter_3_out[7:0]};  // Bit_Extender bit_extender_9
  assign bit_extender_10_out = {{24{1'b0}}, shifter_3_out[7:0]};  // Bit_Extender bit_extender_10
  Multiplexer #(.select(2), .width(32)) multiplexer_13 (
    .in0(adder_1_out), .in1(CSRvaljund), .in2(ALU_valjund), .in3(multiplexer_14_out),
    .out(multiplexer_13_out), .sel(juhise_dekodeerija_1_registri_mux));
  Multiplexer #(.select(3), .width(32)) multiplexer_14 (
    .in0(shifter_3_out), .in1(bit_extender_7_out), .in2(bit_extender_8_out), .in3(bit_extender_9_out),
    .in4(bit_extender_10_out), .out(multiplexer_14_out), .sel(juhise_dekodeerija_1_andmetuup));  // open: in5, in6, in7

  // Other names for the same wires on the sheet: ALUvaljund[31:0] = ALU_valjund

  // Notes on the sheet:
  //   malu_valjund: pull=down
  //   Store/AMO address misaligned
  //   Instruction address misaligned
  //   Store/AMO access fault
  //   Load access fault
  //   Load address misaligned
  //   illegal instruction
  //   Instruction access fault
  //   ECALL
  //   Ebreak
  //   MISA
  //   MVENDORID
  //   MARCID
  //   MIMPID
  //   MHARTID
endmodule

module ALU_RV32IM (
  input  [4:0] Operatsioon,
  input  [31:0] A,
  input  [31:0] B,
  output [31:0] Tulemus
);

  wire adder_1_cout, comparator_1_lt, decoder_1_out1, decoder_1_out2, decoder_1_out11, decoder_1_out13,
       nor_1_out, not_1_out, or_1_out, or_2_out;
  wire [31:0] adder_1_out, and_1_out, bit_extender_1_out, bit_extender_2_out, bit_extender_3_out,
       divider_1_out, divider_1_rem, divider_2_out, divider_2_rem, Korrutaja_1_carry, Korrutaja_1_result,
       multiplexer_1_out, multiplexer_2_out, or_3_out, shifter_1_out, shifter_2_out, shifter_3_out,
       xor_1_out, xor_2_out;

  Decoder #(.enable("false"), .select(5)) decoder_1 (
    .out1(decoder_1_out1), .out2(decoder_1_out2), .out11(decoder_1_out11), .out13(decoder_1_out13),
    .sel(Operatsioon));  // open: out0, out3, out4, out5, out6, out7, out8, out9, out10, out12, out14, out15, out16, out17, out18, out19, out20, out21, out22, out23, out24, out25, out26, out27, out28, out29, out30, out31
  or or_1 (or_1_out, decoder_1_out1, decoder_1_out2);
  assign bit_extender_1_out = {{31{or_1_out}}, or_1_out};  // Bit_Extender bit_extender_1
  or or_2 (or_2_out, decoder_1_out13, decoder_1_out11);
  assign xor_1_out = bit_extender_1_out ^ B;  // XOR_Gate xor_1, 32 bits wide
  Adder #(.width(32)) adder_1 (.a(A), .b(xor_1_out), .out(adder_1_out), .cin(or_1_out), .cout(adder_1_cout));
  not not_1 (not_1_out, adder_1_cout);
  Shifter #(.width(32)) shifter_1 (.in(A), .\dist (B[4:0]), .out(shifter_1_out));
  Shifter #(.shift("lr"), .width(32)) shifter_2 (.in(A), .\dist (B[4:0]), .out(shifter_2_out));
  Shifter #(.shift("ar"), .width(32)) shifter_3 (.in(A), .\dist (B[4:0]), .out(shifter_3_out));
  assign and_1_out = A & B;  // AND_Gate and_1, 32 bits wide
  assign or_3_out = A | B;  // OR_Gate or_3, 32 bits wide
  assign xor_2_out = A ^ B;  // XOR_Gate xor_2, 32 bits wide
  Comparator #(.width(32)) comparator_1 (.a(A), .b(B), .lt(comparator_1_lt));  // open: gt, eq
  Divider #(.width(32)) divider_1 (.a(A), .b(B), .out(divider_1_out), .rem(divider_1_rem));  // open: upper
  Divider #(.mode("twosComplement"), .width(32)) divider_2 (
    .a(A), .b(B), .out(divider_2_out), .rem(divider_2_rem));  // open: upper
  nor nor_1 (nor_1_out, B[31], B[30], B[29], B[28], B[27], B[26], B[25], B[24], B[23], B[22], B[21], B[20], B[19], B[18], B[17], B[16], B[14], B[13], B[12], B[11], B[10], B[9], B[8], B[7], B[6], B[5], B[4], B[3], B[2], B[1], B[0], B[15]);
  assign bit_extender_2_out = {{31{1'b0}}, not_1_out};  // Bit_Extender bit_extender_2
  assign bit_extender_3_out = {{31{1'b0}}, comparator_1_lt};  // Bit_Extender bit_extender_3
  Korrutaja Korrutaja_1 (
    .a_mark(or_2_out), .a(A), .b_mark(decoder_1_out11), .b(B), .result(Korrutaja_1_result),
    .carry(Korrutaja_1_carry));
  Multiplexer #(.width(32)) multiplexer_1 (
    .in0(divider_1_out), .in1({32{1'b1}}), .out(multiplexer_1_out), .sel(nor_1_out));
  Multiplexer #(.width(32)) multiplexer_2 (
    .in0(divider_2_out), .in1({32{1'b1}}), .out(multiplexer_2_out), .sel(nor_1_out));
  // Probe on Operatsioon
  Multiplexer #(.select(5), .width(32)) multiplexer_3 (
    .in0(adder_1_out), .in1(adder_1_out), .in2(bit_extender_2_out), .in3(shifter_1_out), .in4(shifter_2_out),
    .in5(shifter_3_out), .in6(and_1_out), .in7(or_3_out), .in8(xor_2_out), .in9(bit_extender_3_out),
    .in10(Korrutaja_1_result), .in11(Korrutaja_1_carry), .in12(Korrutaja_1_carry), .in13(Korrutaja_1_carry),
    .in14(multiplexer_1_out), .in15(divider_1_rem), .in16(multiplexer_2_out), .in17(divider_2_rem),
    .in18({32{1'b0}}), .in19({32{1'b0}}), .in20({32{1'b0}}), .in21({32{1'b0}}), .in22({32{1'b0}}),
    .in23({32{1'b0}}), .in24({32{1'b0}}), .in25({32{1'b0}}), .in26({32{1'b0}}), .in27({32{1'b0}}),
    .in28({32{1'b0}}), .in29({32{1'b0}}), .in30({32{1'b0}}), .in31({32{1'b0}}), .out(Tulemus),
    .sel(Operatsioon));
endmodule

module Registrid (
  input  [4:0] Aadress_A,
  input  [31:0] Andmed_sisse,
  input  Reset,
  input  Kell,
  input  [4:0] Aadress_B,
  input  [4:0] Write_address,
  output [31:0] Register_A,
  output [31:0] Register_B
);

  wire decoder_1_out1, decoder_1_out2, decoder_1_out3, decoder_1_out4, decoder_1_out5, decoder_1_out6,
       decoder_1_out7, decoder_1_out8, decoder_1_out9, decoder_1_out10, decoder_1_out11, decoder_1_out12,
       decoder_1_out13, decoder_1_out14, decoder_1_out15, decoder_1_out16, decoder_1_out17, decoder_1_out18,
       decoder_1_out19, decoder_1_out20, decoder_1_out21, decoder_1_out22, decoder_1_out23, decoder_1_out24,
       decoder_1_out25, decoder_1_out26, decoder_1_out27, decoder_1_out28, decoder_1_out29, decoder_1_out30,
       decoder_1_out31;
  wire [31:0] X1_q, X2_q, X3_q, X4_q, X5_q, X6_q, X7_q, X8_q, X9_q, X10_q, X11_q, X12_q, X13_q, X14_q, X15_q,
       X16_q, X17_q, X18_q, X19_q, X20_q, X21_q, X22_q, X23_q, X24_q, X25_q, X26_q, X27_q, X28_q, X29_q,
       X30_q, X31_q;

  Decoder #(.enable("false"), .select(5)) decoder_1 (
    .out1(decoder_1_out1), .out2(decoder_1_out2), .out3(decoder_1_out3), .out4(decoder_1_out4),
    .out5(decoder_1_out5), .out6(decoder_1_out6), .out7(decoder_1_out7), .out8(decoder_1_out8),
    .out9(decoder_1_out9), .out10(decoder_1_out10), .out11(decoder_1_out11), .out12(decoder_1_out12),
    .out13(decoder_1_out13), .out14(decoder_1_out14), .out15(decoder_1_out15), .out16(decoder_1_out16),
    .out17(decoder_1_out17), .out18(decoder_1_out18), .out19(decoder_1_out19), .out20(decoder_1_out20),
    .out21(decoder_1_out21), .out22(decoder_1_out22), .out23(decoder_1_out23), .out24(decoder_1_out24),
    .out25(decoder_1_out25), .out26(decoder_1_out26), .out27(decoder_1_out27), .out28(decoder_1_out28),
    .out29(decoder_1_out29), .out30(decoder_1_out30), .out31(decoder_1_out31), .sel(Write_address));  // open: out0
  Register #(.width(32)) X28 (.D(Andmed_sisse), .en(decoder_1_out28), .clk(Kell), .Q(X28_q), .clr(Reset));
  Register #(.width(32)) X29 (.D(Andmed_sisse), .en(decoder_1_out29), .clk(Kell), .Q(X29_q), .clr(Reset));
  Register #(.width(32)) X30 (.D(Andmed_sisse), .en(decoder_1_out30), .clk(Kell), .Q(X30_q), .clr(Reset));
  Register #(.width(32)) X31 (.D(Andmed_sisse), .en(decoder_1_out31), .clk(Kell), .Q(X31_q), .clr(Reset));
  Register #(.width(32)) X24 (.D(Andmed_sisse), .en(decoder_1_out24), .clk(Kell), .Q(X24_q), .clr(Reset));
  Register #(.width(32)) X25 (.D(Andmed_sisse), .en(decoder_1_out25), .clk(Kell), .Q(X25_q), .clr(Reset));
  Register #(.width(32)) X26 (.D(Andmed_sisse), .en(decoder_1_out26), .clk(Kell), .Q(X26_q), .clr(Reset));
  Register #(.width(32)) X27 (.D(Andmed_sisse), .en(decoder_1_out27), .clk(Kell), .Q(X27_q), .clr(Reset));
  Register #(.width(32)) X20 (.D(Andmed_sisse), .en(decoder_1_out20), .clk(Kell), .Q(X20_q), .clr(Reset));
  Register #(.width(32)) X21 (.D(Andmed_sisse), .en(decoder_1_out21), .clk(Kell), .Q(X21_q), .clr(Reset));
  Register #(.width(32)) X22 (.D(Andmed_sisse), .en(decoder_1_out22), .clk(Kell), .Q(X22_q), .clr(Reset));
  Register #(.width(32)) X23 (.D(Andmed_sisse), .en(decoder_1_out23), .clk(Kell), .Q(X23_q), .clr(Reset));
  Register #(.width(32)) X16 (.D(Andmed_sisse), .en(decoder_1_out16), .clk(Kell), .Q(X16_q), .clr(Reset));
  Register #(.width(32)) X17 (.D(Andmed_sisse), .en(decoder_1_out17), .clk(Kell), .Q(X17_q), .clr(Reset));
  Register #(.width(32)) X18 (.D(Andmed_sisse), .en(decoder_1_out18), .clk(Kell), .Q(X18_q), .clr(Reset));
  Register #(.width(32)) X19 (.D(Andmed_sisse), .en(decoder_1_out19), .clk(Kell), .Q(X19_q), .clr(Reset));
  Register #(.width(32)) X12 (.D(Andmed_sisse), .en(decoder_1_out12), .clk(Kell), .Q(X12_q), .clr(Reset));
  Register #(.width(32)) X13 (.D(Andmed_sisse), .en(decoder_1_out13), .clk(Kell), .Q(X13_q), .clr(Reset));
  Register #(.width(32)) X14 (.D(Andmed_sisse), .en(decoder_1_out14), .clk(Kell), .Q(X14_q), .clr(Reset));
  Register #(.width(32)) X15 (.D(Andmed_sisse), .en(decoder_1_out15), .clk(Kell), .Q(X15_q), .clr(Reset));
  Register #(.width(32)) X8 (.D(Andmed_sisse), .en(decoder_1_out8), .clk(Kell), .Q(X8_q), .clr(Reset));
  Register #(.width(32)) X9 (.D(Andmed_sisse), .en(decoder_1_out9), .clk(Kell), .Q(X9_q), .clr(Reset));
  Register #(.width(32)) X10 (.D(Andmed_sisse), .en(decoder_1_out10), .clk(Kell), .Q(X10_q), .clr(Reset));
  Register #(.width(32)) X11 (.D(Andmed_sisse), .en(decoder_1_out11), .clk(Kell), .Q(X11_q), .clr(Reset));
  Register #(.width(32)) X4 (.D(Andmed_sisse), .en(decoder_1_out4), .clk(Kell), .Q(X4_q), .clr(Reset));
  Register #(.width(32)) X5 (.D(Andmed_sisse), .en(decoder_1_out5), .clk(Kell), .Q(X5_q), .clr(Reset));
  Register #(.width(32)) X6 (.D(Andmed_sisse), .en(decoder_1_out6), .clk(Kell), .Q(X6_q), .clr(Reset));
  Register #(.width(32)) X7 (.D(Andmed_sisse), .en(decoder_1_out7), .clk(Kell), .Q(X7_q), .clr(Reset));
  Register #(.width(32)) X1 (.D(Andmed_sisse), .en(decoder_1_out1), .clk(Kell), .Q(X1_q), .clr(Reset));
  Register #(.width(32)) X2 (.D(Andmed_sisse), .en(decoder_1_out2), .clk(Kell), .Q(X2_q), .clr(Reset));
  Register #(.width(32)) X3 (.D(Andmed_sisse), .en(decoder_1_out3), .clk(Kell), .Q(X3_q), .clr(Reset));
  Multiplexer #(.select(5), .width(32)) multiplexer_1 (
    .in0({32{1'b0}}), .in1(X1_q), .in2(X2_q), .in3(X3_q), .in4(X4_q), .in5(X5_q), .in6(X6_q), .in7(X7_q),
    .in8(X8_q), .in9(X9_q), .in10(X10_q), .in11(X11_q), .in12(X12_q), .in13(X13_q), .in14(X14_q),
    .in15(X15_q), .in16(X16_q), .in17(X17_q), .in18(X18_q), .in19(X19_q), .in20(X20_q), .in21(X21_q),
    .in22(X22_q), .in23(X23_q), .in24(X24_q), .in25(X25_q), .in26(X26_q), .in27(X27_q), .in28(X28_q),
    .in29(X29_q), .in30(X30_q), .in31(X31_q), .out(Register_A), .sel(Aadress_A));
  Multiplexer #(.select(5), .width(32)) multiplexer_2 (
    .in0({32{1'b0}}), .in1(X1_q), .in2(X2_q), .in3(X3_q), .in4(X4_q), .in5(X5_q), .in6(X6_q), .in7(X7_q),
    .in8(X8_q), .in9(X9_q), .in10(X10_q), .in11(X11_q), .in12(X12_q), .in13(X13_q), .in14(X14_q),
    .in15(X15_q), .in16(X16_q), .in17(X17_q), .in18(X18_q), .in19(X19_q), .in20(X20_q), .in21(X21_q),
    .in22(X22_q), .in23(X23_q), .in24(X24_q), .in25(X25_q), .in26(X26_q), .in27(X27_q), .in28(X28_q),
    .in29(X29_q), .in30(X30_q), .in31(X31_q), .out(Register_B), .sel(Aadress_B));

  // Notes on the sheet:
  //   X0
endmodule

module Juhise_dekodeerija (
  input  [31:0] Juhis,
  output [31:0] Otsene,
  output [4:0] Operatsioon,
  output [1:0] Registri_mux,
  output ALU_sisend_A,
  output [4:0] rsA,
  output [4:0] rsB,
  output [4:0] rd,
  output [2:0] andmetuup,
  output ALU_sisend_B,
  output Luba_kirjutamine,
  output CSR_luba_kirjutamine,
  output [11:0] CSR_aadress,
  output mret,
  output Hargnemise_valik,
  output [2:0] PC_kontroll,
  output [2:0] erindid
);

  wire ALU_src_A, ALU_src_B, and_1_out, and_2_out, and_3_out, and_4_out, and_5_out, and_6_out, and_7_out,
       and_8_out, and_9_out, and_10_out, and_11_out, and_12_out, and_13_out, and_14_out, and_15_out,
       and_16_out, and_17_out, and_18_out, and_19_out, and_20_out, and_21_out, and_22_out, and_23_out,
       and_24_out, and_25_out, and_26_out, and_27_out, and_28_out, and_29_out, and_30_out, and_31_out,
       and_32_out, and_33_out, and_34_out, and_35_out, and_36_out, and_37_out, and_38_out, and_39_out,
       and_40_out, and_41_out, and_42_out, and_43_out, and_44_out, and_45_out, and_46_out, and_47_out,
       and_48_out, and_49_out, and_50_out, and_51_out, and_52_out, and_56_out, and_57_out, and_58_out,
       and_59_out, and_60_out, and_61_out, and_62_out, and_63_out, and_64_out, and_65_out, Branch_select,
       CSR_write_enable, kehtiv, or_1_out, or_2_out, or_3_out, or_4_out, or_5_out, or_6_out, or_7_out,
       or_8_out, or_9_out, or_10_out, or_11_out, or_12_out, or_13_out, or_14_out, or_15_out, or_16_out,
       or_17_out, or_18_out, or_19_out, or_20_out, or_21_out, or_22_out, or_23_out, or_24_out, or_25_out,
       or_26_out, or_27_out, or_28_out, or_29_out, or_30_out, or_31_out, or_32_out, or_33_out, or_34_out,
       or_35_out, or_36_out, or_37_out, or_38_out, or_39_out, or_40_out, or_41_out, or_42_out, or_43_out,
       or_44_out, or_45_out, or_46_out, or_47_out, or_48_out, or_49_out, or_50_out, or_51_out, or_52_out,
       or_53_out, or_54_out, undriven, Write_enable;
  wire [1:0] Register_mux;
  wire [2:0] Data_type, PC_ctrl;
  wire [4:0] Command, rd_t, rs1, rs2;
  wire [11:0] bit_extender_3_out, CSR_address;
  wire [31:0] bit_extender_1_out, bit_extender_2_out, bit_extender_4_out, bit_extender_5_out,
       bit_extender_6_out, bit_extender_7_out, Immidiate;

  and and_1 (and_1_out, Juhis[0], Juhis[1], ~Juhis[2], ~Juhis[3], Juhis[4], Juhis[5], ~Juhis[6]);  // AND_Gate
  // Probe on undriven
  or or_1 (or_1_out, and_2_out, or_2_out);
  and and_2 (and_2_out, Juhis[0], Juhis[1], ~Juhis[2], ~Juhis[3], Juhis[4], Juhis[5], ~Juhis[6], ~Juhis[12], ~Juhis[13], ~Juhis[14], ~Juhis[25], ~Juhis[26], ~Juhis[27], ~Juhis[28], ~Juhis[29], ~Juhis[30], ~Juhis[31]);  // AND_Gate
  or or_2 (or_2_out, and_3_out, or_3_out);
  and and_3 (and_3_out, Juhis[0], Juhis[1], ~Juhis[2], ~Juhis[3], Juhis[4], Juhis[5], ~Juhis[6], ~Juhis[12], ~Juhis[13], ~Juhis[14], ~Juhis[25], ~Juhis[26], ~Juhis[27], ~Juhis[28], ~Juhis[29], Juhis[30], ~Juhis[31]);  // AND_Gate
  and and_4 (and_4_out, Juhis[0], Juhis[1], ~Juhis[2], ~Juhis[3], Juhis[4], Juhis[5], ~Juhis[6], Juhis[12], Juhis[13], Juhis[14], ~Juhis[25], ~Juhis[26], ~Juhis[27], ~Juhis[28], ~Juhis[29], ~Juhis[30], ~Juhis[31]);  // AND_Gate
  and and_5 (and_5_out, Juhis[0], Juhis[1], ~Juhis[2], ~Juhis[3], Juhis[4], Juhis[5], ~Juhis[6], ~Juhis[12], Juhis[13], Juhis[14], ~Juhis[25], ~Juhis[26], ~Juhis[27], ~Juhis[28], ~Juhis[29], ~Juhis[30], ~Juhis[31]);  // AND_Gate
  and and_6 (and_6_out, Juhis[0], Juhis[1], ~Juhis[2], ~Juhis[3], Juhis[4], Juhis[5], ~Juhis[6], ~Juhis[12], ~Juhis[13], Juhis[14], ~Juhis[25], ~Juhis[26], ~Juhis[27], ~Juhis[28], ~Juhis[29], ~Juhis[30], ~Juhis[31]);  // AND_Gate
  and and_7 (and_7_out, Juhis[0], Juhis[1], ~Juhis[2], ~Juhis[3], Juhis[4], Juhis[5], ~Juhis[6], Juhis[12], ~Juhis[13], ~Juhis[14], ~Juhis[25], ~Juhis[26], ~Juhis[27], ~Juhis[28], ~Juhis[29], ~Juhis[30], ~Juhis[31]);  // AND_Gate
  and and_8 (and_8_out, Juhis[0], Juhis[1], ~Juhis[2], ~Juhis[3], Juhis[4], Juhis[5], ~Juhis[6], ~Juhis[12], Juhis[13], ~Juhis[14], ~Juhis[25], ~Juhis[26], ~Juhis[27], ~Juhis[28], ~Juhis[29], ~Juhis[30], ~Juhis[31]);  // AND_Gate
  and and_9 (and_9_out, Juhis[0], Juhis[1], ~Juhis[2], ~Juhis[3], Juhis[4], Juhis[5], ~Juhis[6], Juhis[12], Juhis[13], ~Juhis[14], ~Juhis[25], ~Juhis[26], ~Juhis[27], ~Juhis[28], ~Juhis[29], ~Juhis[30], ~Juhis[31]);  // AND_Gate
  and and_10 (and_10_out, Juhis[0], Juhis[1], ~Juhis[2], ~Juhis[3], Juhis[4], Juhis[5], ~Juhis[6], Juhis[12], ~Juhis[13], Juhis[14], ~Juhis[25], ~Juhis[26], ~Juhis[27], ~Juhis[28], ~Juhis[29], ~Juhis[30], ~Juhis[31]);  // AND_Gate
  and and_11 (and_11_out, Juhis[0], Juhis[1], ~Juhis[2], ~Juhis[3], Juhis[4], Juhis[5], ~Juhis[6], Juhis[12], ~Juhis[13], Juhis[14], ~Juhis[25], ~Juhis[26], ~Juhis[27], ~Juhis[28], ~Juhis[29], Juhis[30], ~Juhis[31]);  // AND_Gate
  and and_12 (and_12_out, Juhis[0], Juhis[1], ~Juhis[2], ~Juhis[3], Juhis[4], Juhis[5], ~Juhis[6], ~Juhis[12], ~Juhis[13], ~Juhis[14], Juhis[25], ~Juhis[26], ~Juhis[27], ~Juhis[28], ~Juhis[29], ~Juhis[30], ~Juhis[31]);  // AND_Gate
  and and_13 (and_13_out, Juhis[0], Juhis[1], ~Juhis[2], ~Juhis[3], Juhis[4], Juhis[5], ~Juhis[6], Juhis[12], ~Juhis[13], ~Juhis[14], Juhis[25], ~Juhis[26], ~Juhis[27], ~Juhis[28], ~Juhis[29], ~Juhis[30], ~Juhis[31]);  // AND_Gate
  and and_14 (and_14_out, Juhis[0], Juhis[1], ~Juhis[2], ~Juhis[3], Juhis[4], Juhis[5], ~Juhis[6], Juhis[12], Juhis[13], ~Juhis[14], Juhis[25], ~Juhis[26], ~Juhis[27], ~Juhis[28], ~Juhis[29], ~Juhis[30], ~Juhis[31]);  // AND_Gate
  and and_15 (and_15_out, Juhis[0], Juhis[1], ~Juhis[2], ~Juhis[3], Juhis[4], Juhis[5], ~Juhis[6], ~Juhis[12], Juhis[13], ~Juhis[14], Juhis[25], ~Juhis[26], ~Juhis[27], ~Juhis[28], ~Juhis[29], ~Juhis[30], ~Juhis[31]);  // AND_Gate
  and and_16 (and_16_out, Juhis[0], Juhis[1], ~Juhis[2], ~Juhis[3], Juhis[4], Juhis[5], ~Juhis[6], Juhis[12], ~Juhis[13], Juhis[14], Juhis[25], ~Juhis[26], ~Juhis[27], ~Juhis[28], ~Juhis[29], ~Juhis[30], ~Juhis[31]);  // AND_Gate
  and and_17 (and_17_out, Juhis[0], Juhis[1], ~Juhis[2], ~Juhis[3], Juhis[4], Juhis[5], ~Juhis[6], Juhis[12], Juhis[13], Juhis[14], Juhis[25], ~Juhis[26], ~Juhis[27], ~Juhis[28], ~Juhis[29], ~Juhis[30], ~Juhis[31]);  // AND_Gate
  and and_18 (and_18_out, Juhis[0], Juhis[1], ~Juhis[2], ~Juhis[3], Juhis[4], Juhis[5], ~Juhis[6], ~Juhis[12], ~Juhis[13], Juhis[14], Juhis[25], ~Juhis[26], ~Juhis[27], ~Juhis[28], ~Juhis[29], ~Juhis[30], ~Juhis[31]);  // AND_Gate
  and and_19 (and_19_out, Juhis[0], Juhis[1], ~Juhis[2], ~Juhis[3], Juhis[4], Juhis[5], ~Juhis[6], ~Juhis[12], Juhis[13], Juhis[14], Juhis[25], ~Juhis[26], ~Juhis[27], ~Juhis[28], ~Juhis[29], ~Juhis[30], ~Juhis[31]);  // AND_Gate
  or or_3 (or_3_out, and_4_out, or_4_out);
  or or_4 (or_4_out, and_5_out, or_5_out);
  or or_5 (or_5_out, and_6_out, or_6_out);
  or or_6 (or_6_out, and_7_out, or_7_out);
  or or_7 (or_7_out, and_8_out, or_8_out);
  or or_8 (or_8_out, and_9_out, or_9_out);
  or or_9 (or_9_out, and_10_out, or_10_out);
  or or_10 (or_10_out, and_11_out, or_17_out);
  or or_11 (or_11_out, and_13_out, or_12_out);
  or or_12 (or_12_out, and_14_out, or_13_out);
  or or_13 (or_13_out, and_15_out, or_14_out);
  or or_14 (or_14_out, and_16_out, or_18_out);
  or or_15 (or_15_out, or_16_out, and_18_out);
  buf or_16 (or_16_out, and_19_out);  // OR_Gate
  assign rd_t = and_1_out ? Juhis[11:7] : 5'bz;  // Controlled_Buffer controlled_buffer_1
  assign rs1 = and_1_out ? Juhis[19:15] : 5'bz;  // Controlled_Buffer controlled_buffer_2
  assign rs2 = and_1_out ? Juhis[24:20] : 5'bz;  // Controlled_Buffer controlled_buffer_3
  assign ALU_src_B = and_1_out ? 1'b0 : 1'bz;  // Controlled_Buffer controlled_buffer_4
  assign Write_enable = and_1_out ? 1'b0 : 1'bz;  // Controlled_Buffer controlled_buffer_5
  assign ALU_src_A = and_1_out ? 1'b1 : 1'bz;  // Controlled_Buffer controlled_buffer_6
  assign Data_type = and_1_out ? 3'b000 : 3'bz;  // Controlled_Buffer controlled_buffer_7
  assign Register_mux = and_1_out ? 2'b10 : 2'bz;  // Controlled_Buffer controlled_buffer_8
  assign CSR_write_enable = and_1_out ? 1'b0 : 1'bz;  // Controlled_Buffer controlled_buffer_9
  assign CSR_address = and_1_out ? {12{1'b0}} : 12'bz;  // Controlled_Buffer controlled_buffer_10
  assign PC_ctrl = and_1_out ? 3'b000 : 3'bz;  // Controlled_Buffer controlled_buffer_11
  assign Command = and_2_out ? {5{1'b0}} : 5'bz;  // Controlled_Buffer controlled_buffer_12
  assign Command = and_3_out ? 5'b00001 : 5'bz;  // Controlled_Buffer controlled_buffer_13
  assign Command = and_4_out ? 5'b00110 : 5'bz;  // Controlled_Buffer controlled_buffer_14
  assign Command = and_5_out ? 5'b00111 : 5'bz;  // Controlled_Buffer controlled_buffer_15
  assign Command = and_6_out ? 5'b01000 : 5'bz;  // Controlled_Buffer controlled_buffer_16
  assign Command = and_7_out ? 5'b00011 : 5'bz;  // Controlled_Buffer controlled_buffer_17
  assign Command = and_8_out ? 5'b01001 : 5'bz;  // Controlled_Buffer controlled_buffer_18
  assign Command = and_9_out ? 5'b00010 : 5'bz;  // Controlled_Buffer controlled_buffer_19
  assign Command = and_10_out ? 5'b00100 : 5'bz;  // Controlled_Buffer controlled_buffer_20
  assign Command = and_11_out ? 5'b00101 : 5'bz;  // Controlled_Buffer controlled_buffer_21
  or or_17 (or_17_out, and_12_out, or_11_out);
  assign Command = and_12_out ? 5'b01010 : 5'bz;  // Controlled_Buffer controlled_buffer_22
  assign Command = and_13_out ? 5'b01011 : 5'bz;  // Controlled_Buffer controlled_buffer_23
  assign Command = and_14_out ? 5'b01100 : 5'bz;  // Controlled_Buffer controlled_buffer_24
  assign Command = and_15_out ? 5'b01101 : 5'bz;  // Controlled_Buffer controlled_buffer_25
  assign Command = and_16_out ? 5'b01110 : 5'bz;  // Controlled_Buffer controlled_buffer_26
  or or_18 (or_18_out, or_15_out, and_17_out);
  assign Command = and_17_out ? 5'b01111 : 5'bz;  // Controlled_Buffer controlled_buffer_27
  assign Command = and_18_out ? 5'b10000 : 5'bz;  // Controlled_Buffer controlled_buffer_28
  assign Command = and_19_out ? 5'b10001 : 5'bz;  // Controlled_Buffer controlled_buffer_29
  and and_20 (and_20_out, Juhis[0], Juhis[1], Juhis[2], ~Juhis[3], Juhis[4], Juhis[5], ~Juhis[6]);  // AND_Gate
  and and_21 (and_21_out, Juhis[0], Juhis[1], Juhis[2], ~Juhis[3], Juhis[4], ~Juhis[5], ~Juhis[6]);  // AND_Gate
  or or_19 (or_19_out, and_21_out, and_20_out);
  or or_20 (or_20_out, or_1_out, or_19_out);
  assign rd_t = and_20_out ? Juhis[11:7] : 5'bz;  // Controlled_Buffer controlled_buffer_30
  assign Immidiate = and_20_out ? {Juhis[31:12], {12{1'b0}}} : 32'bz;  // Controlled_Buffer controlled_buffer_31
  assign rs1 = and_20_out ? {5{1'b0}} : 5'bz;  // Controlled_Buffer controlled_buffer_32
  assign rd_t = and_21_out ? Juhis[11:7] : 5'bz;  // Controlled_Buffer controlled_buffer_33
  assign Immidiate = and_21_out ? {Juhis[31:12], {12{1'b0}}} : 32'bz;  // Controlled_Buffer controlled_buffer_34
  assign rs1 = and_21_out ? {5{1'b0}} : 5'bz;  // Controlled_Buffer controlled_buffer_35
  assign rs2 = and_20_out ? {5{1'b0}} : 5'bz;  // Controlled_Buffer controlled_buffer_36
  assign Command = and_20_out ? 5'b00111 : 5'bz;  // Controlled_Buffer controlled_buffer_37
  assign Register_mux = and_20_out ? 2'b10 : 2'bz;  // Controlled_Buffer controlled_buffer_38
  assign ALU_src_B = and_20_out ? 1'b1 : 1'bz;  // Controlled_Buffer controlled_buffer_39
  assign CSR_write_enable = and_20_out ? 1'b0 : 1'bz;  // Controlled_Buffer controlled_buffer_40
  assign CSR_address = and_20_out ? {12{1'b0}} : 12'bz;  // Controlled_Buffer controlled_buffer_41
  assign PC_ctrl = and_20_out ? 3'b000 : 3'bz;  // Controlled_Buffer controlled_buffer_42
  assign rs2 = and_21_out ? {5{1'b0}} : 5'bz;  // Controlled_Buffer controlled_buffer_43
  assign Command = and_21_out ? 5'b00111 : 5'bz;  // Controlled_Buffer controlled_buffer_44
  assign Register_mux = and_21_out ? 2'b10 : 2'bz;  // Controlled_Buffer controlled_buffer_45
  assign ALU_src_B = and_21_out ? 1'b1 : 1'bz;  // Controlled_Buffer controlled_buffer_46
  assign CSR_write_enable = and_21_out ? 1'b0 : 1'bz;  // Controlled_Buffer controlled_buffer_47
  assign CSR_address = and_21_out ? {12{1'b0}} : 12'bz;  // Controlled_Buffer controlled_buffer_48
  assign PC_ctrl = and_21_out ? 3'b000 : 3'bz;  // Controlled_Buffer controlled_buffer_49
  assign Write_enable = and_20_out ? 1'b0 : 1'bz;  // Controlled_Buffer controlled_buffer_50
  assign Data_type = and_20_out ? 3'b000 : 3'bz;  // Controlled_Buffer controlled_buffer_51
  assign ALU_src_A = and_20_out ? 1'b1 : 1'bz;  // Controlled_Buffer controlled_buffer_52
  assign Write_enable = and_21_out ? 1'b0 : 1'bz;  // Controlled_Buffer controlled_buffer_53
  assign Data_type = and_21_out ? 3'b000 : 3'bz;  // Controlled_Buffer controlled_buffer_54
  assign ALU_src_A = and_21_out ? 1'b0 : 1'bz;  // Controlled_Buffer controlled_buffer_55
  and and_22 (and_22_out, Juhis[0], Juhis[1], ~Juhis[2], ~Juhis[3], Juhis[4], ~Juhis[5], ~Juhis[6]);  // AND_Gate
  and and_23 (and_23_out, Juhis[0], Juhis[1], ~Juhis[2], ~Juhis[3], Juhis[4], ~Juhis[5], ~Juhis[6], ~Juhis[12], ~Juhis[13], ~Juhis[14]);  // AND_Gate
  and and_24 (and_24_out, Juhis[0], Juhis[1], ~Juhis[2], ~Juhis[3], Juhis[4], ~Juhis[5], ~Juhis[6], ~Juhis[12], Juhis[13], ~Juhis[14]);  // AND_Gate
  and and_25 (and_25_out, Juhis[0], Juhis[1], ~Juhis[2], ~Juhis[3], Juhis[4], ~Juhis[5], ~Juhis[6], Juhis[12], Juhis[13], ~Juhis[14]);  // AND_Gate
  and and_26 (and_26_out, Juhis[0], Juhis[1], ~Juhis[2], ~Juhis[3], Juhis[4], ~Juhis[5], ~Juhis[6], ~Juhis[12], ~Juhis[13], Juhis[14]);  // AND_Gate
  and and_27 (and_27_out, Juhis[0], Juhis[1], ~Juhis[2], ~Juhis[3], Juhis[4], ~Juhis[5], ~Juhis[6], ~Juhis[12], Juhis[13], Juhis[14]);  // AND_Gate
  and and_28 (and_28_out, Juhis[0], Juhis[1], ~Juhis[2], ~Juhis[3], Juhis[4], ~Juhis[5], ~Juhis[6], Juhis[12], Juhis[13], Juhis[14]);  // AND_Gate
  and and_29 (and_29_out, Juhis[0], Juhis[1], ~Juhis[2], ~Juhis[3], Juhis[4], ~Juhis[5], ~Juhis[6], Juhis[12], ~Juhis[13], ~Juhis[14]);  // AND_Gate
  and and_30 (and_30_out, Juhis[0], Juhis[1], ~Juhis[2], ~Juhis[3], Juhis[4], ~Juhis[5], ~Juhis[6], Juhis[12], ~Juhis[13], Juhis[14]);  // AND_Gate
  assign bit_extender_1_out = {{20{Juhis[31]}}, Juhis[31:20]};  // Bit_Extender bit_extender_1
  and and_31 (and_31_out, ~bit_extender_1_out[31], ~bit_extender_1_out[30], ~bit_extender_1_out[29], ~bit_extender_1_out[28], ~bit_extender_1_out[27]);  // AND_Gate
  and and_32 (and_32_out, and_31_out, and_30_out);
  and and_33 (and_33_out, ~bit_extender_1_out[31], ~bit_extender_1_out[30], ~bit_extender_1_out[29], bit_extender_1_out[28], ~bit_extender_1_out[27]);  // AND_Gate
  and and_34 (and_34_out, and_33_out, and_30_out);
  or or_21 (or_21_out, and_23_out, or_22_out);
  or or_22 (or_22_out, or_23_out, and_24_out);
  or or_23 (or_23_out, and_25_out, or_24_out);
  or or_24 (or_24_out, or_25_out, and_26_out);
  or or_25 (or_25_out, and_27_out, or_26_out);
  or or_26 (or_26_out, or_27_out, and_28_out);
  or or_27 (or_27_out, and_29_out, or_28_out);
  or or_28 (or_28_out, and_34_out, and_32_out);
  or or_29 (or_29_out, or_20_out, or_21_out);
  assign rd_t = and_22_out ? Juhis[11:7] : 5'bz;  // Controlled_Buffer controlled_buffer_56
  assign rs1 = and_22_out ? Juhis[19:15] : 5'bz;  // Controlled_Buffer controlled_buffer_57
  assign rs2 = and_22_out ? {5{1'b0}} : 5'bz;  // Controlled_Buffer controlled_buffer_58
  assign Immidiate = and_22_out ? bit_extender_1_out : 32'bz;  // Controlled_Buffer controlled_buffer_59
  assign ALU_src_A = and_22_out ? 1'b1 : 1'bz;  // Controlled_Buffer controlled_buffer_60
  assign Write_enable = and_22_out ? 1'b0 : 1'bz;  // Controlled_Buffer controlled_buffer_61
  assign Data_type = and_22_out ? 3'b000 : 3'bz;  // Controlled_Buffer controlled_buffer_62
  assign Register_mux = and_22_out ? 2'b10 : 2'bz;  // Controlled_Buffer controlled_buffer_63
  assign CSR_write_enable = and_22_out ? 1'b0 : 1'bz;  // Controlled_Buffer controlled_buffer_64
  assign ALU_src_B = and_22_out ? 1'b1 : 1'bz;  // Controlled_Buffer controlled_buffer_65
  assign CSR_address = and_22_out ? {12{1'b0}} : 12'bz;  // Controlled_Buffer controlled_buffer_66
  assign PC_ctrl = and_22_out ? 3'b000 : 3'bz;  // Controlled_Buffer controlled_buffer_67
  assign Branch_select = and_22_out ? 1'b0 : 1'bz;  // Controlled_Buffer controlled_buffer_68
  assign Command = and_23_out ? {5{1'b0}} : 5'bz;  // Controlled_Buffer controlled_buffer_69
  assign Command = and_24_out ? 5'b01001 : 5'bz;  // Controlled_Buffer controlled_buffer_70
  assign Command = and_25_out ? 5'b00010 : 5'bz;  // Controlled_Buffer controlled_buffer_71
  assign Command = and_26_out ? 5'b01000 : 5'bz;  // Controlled_Buffer controlled_buffer_72
  assign Command = and_27_out ? 5'b00111 : 5'bz;  // Controlled_Buffer controlled_buffer_73
  assign Command = and_28_out ? 5'b00110 : 5'bz;  // Controlled_Buffer controlled_buffer_74
  assign Command = and_29_out ? 5'b00011 : 5'bz;  // Controlled_Buffer controlled_buffer_75
  assign Command = and_32_out ? 5'b00100 : 5'bz;  // Controlled_Buffer controlled_buffer_76
  assign Command = and_34_out ? 5'b00101 : 5'bz;  // Controlled_Buffer controlled_buffer_77
  and and_35 (and_35_out, Juhis[0], Juhis[1], ~Juhis[2], ~Juhis[3], Juhis[4], Juhis[5], Juhis[6]);  // AND_Gate
  or or_30 (or_30_out, Juhis[12], Juhis[13], Juhis[14]);
  and and_36 (and_36_out, Juhis[0], Juhis[1], ~Juhis[2], ~Juhis[3], Juhis[4], Juhis[5], Juhis[6], Juhis[12], ~Juhis[13], ~Juhis[14]);  // AND_Gate
  and and_37 (and_37_out, Juhis[0], Juhis[1], ~Juhis[2], ~Juhis[3], Juhis[4], Juhis[5], Juhis[6], ~Juhis[12], Juhis[13], ~Juhis[14]);  // AND_Gate
  and and_38 (and_38_out, Juhis[0], Juhis[1], ~Juhis[2], ~Juhis[3], Juhis[4], Juhis[5], Juhis[6], Juhis[12], Juhis[13], ~Juhis[14]);  // AND_Gate
  and and_39 (and_39_out, Juhis[0], Juhis[1], ~Juhis[2], ~Juhis[3], Juhis[4], Juhis[5], Juhis[6], Juhis[12], ~Juhis[13], Juhis[14]);  // AND_Gate
  and and_40 (and_40_out, Juhis[0], Juhis[1], ~Juhis[2], ~Juhis[3], Juhis[4], Juhis[5], Juhis[6], ~Juhis[12], Juhis[13], Juhis[14]);  // AND_Gate
  and and_41 (and_41_out, Juhis[0], Juhis[1], ~Juhis[2], ~Juhis[3], Juhis[4], Juhis[5], Juhis[6], Juhis[12], Juhis[13], Juhis[14]);  // AND_Gate
  and and_42 (and_42_out, and_35_out, or_30_out);
  or or_31 (or_31_out, or_32_out, and_36_out);
  or or_32 (or_32_out, or_33_out, and_37_out);
  or or_33 (or_33_out, or_34_out, and_38_out);
  or or_34 (or_34_out, or_35_out, and_39_out);
  or or_35 (or_35_out, and_41_out, and_40_out);
  assign bit_extender_2_out = {{27{1'b0}}, Juhis[24:20]};  // Bit_Extender bit_extender_2
  assign rd_t = and_42_out ? Juhis[11:7] : 5'bz;  // Controlled_Buffer controlled_buffer_78
  assign rs1 = and_42_out ? Juhis[19:15] : 5'bz;  // Controlled_Buffer controlled_buffer_79
  assign rs2 = and_42_out ? {5{1'b0}} : 5'bz;  // Controlled_Buffer controlled_buffer_80
  assign CSR_address = and_42_out ? Juhis[31:20] : 12'bz;  // Controlled_Buffer controlled_buffer_81
  assign Immidiate = and_42_out ? bit_extender_2_out : 32'bz;  // Controlled_Buffer controlled_buffer_82
  assign ALU_src_A = and_42_out ? 1'b1 : 1'bz;  // Controlled_Buffer controlled_buffer_83
  assign CSR_write_enable = and_42_out ? 1'b1 : 1'bz;  // Controlled_Buffer controlled_buffer_84
  assign Write_enable = and_42_out ? 1'b0 : 1'bz;  // Controlled_Buffer controlled_buffer_85
  assign Data_type = and_42_out ? 3'b000 : 3'bz;  // Controlled_Buffer controlled_buffer_86
  assign Register_mux = and_42_out ? 2'b01 : 2'bz;  // Controlled_Buffer controlled_buffer_87
  assign PC_ctrl = and_42_out ? 3'b000 : 3'bz;  // Controlled_Buffer controlled_buffer_88
  assign Command = and_36_out ? {5{1'b0}} : 5'bz;  // Controlled_Buffer controlled_buffer_89
  assign ALU_src_B = and_36_out ? 1'b0 : 1'bz;  // Controlled_Buffer controlled_buffer_90
  assign Command = and_37_out ? 5'b00111 : 5'bz;  // Controlled_Buffer controlled_buffer_91
  assign ALU_src_B = and_37_out ? 1'b0 : 1'bz;  // Controlled_Buffer controlled_buffer_92
  assign Command = and_38_out ? 5'b01000 : 5'bz;  // Controlled_Buffer controlled_buffer_93
  assign ALU_src_B = and_38_out ? 1'b0 : 1'bz;  // Controlled_Buffer controlled_buffer_94
  assign Command = and_39_out ? {5{1'b0}} : 5'bz;  // Controlled_Buffer controlled_buffer_95
  assign ALU_src_B = and_39_out ? 1'b1 : 1'bz;  // Controlled_Buffer controlled_buffer_96
  assign Command = and_40_out ? 5'b00111 : 5'bz;  // Controlled_Buffer controlled_buffer_97
  assign ALU_src_B = and_40_out ? 1'b1 : 1'bz;  // Controlled_Buffer controlled_buffer_98
  assign Command = and_41_out ? 5'b01000 : 5'bz;  // Controlled_Buffer controlled_buffer_99
  assign ALU_src_B = and_41_out ? 1'b1 : 1'bz;  // Controlled_Buffer controlled_buffer_100
  or or_36 (or_36_out, or_29_out, or_31_out);
  assign bit_extender_3_out = {{11{Juhis[31]}}, Juhis[31]};  // Bit_Extender bit_extender_3
  and and_43 (and_43_out, Juhis[0], Juhis[1], Juhis[2], Juhis[3], ~Juhis[4], Juhis[5], Juhis[6]);  // AND_Gate
  and and_44 (and_44_out, Juhis[0], Juhis[1], Juhis[2], ~Juhis[3], ~Juhis[4], Juhis[5], Juhis[6], ~Juhis[12], ~Juhis[13], ~Juhis[14]);  // AND_Gate
  assign bit_extender_4_out = {{20{Juhis[31]}}, Juhis[31:20]};  // Bit_Extender bit_extender_4
  assign Immidiate = and_43_out ? {bit_extender_3_out, Juhis[19:12], Juhis[20], Juhis[30:21], 1'b0} : 32'bz;  // Controlled_Buffer controlled_buffer_101
  assign Command = and_43_out ? {5{1'b0}} : 5'bz;  // Controlled_Buffer controlled_buffer_102
  assign Register_mux = and_43_out ? 2'b00 : 2'bz;  // Controlled_Buffer controlled_buffer_103
  assign ALU_src_A = and_43_out ? 1'b0 : 1'bz;  // Controlled_Buffer controlled_buffer_104
  assign rs1 = and_43_out ? {5{1'b0}} : 5'bz;  // Controlled_Buffer controlled_buffer_105
  assign rs2 = and_43_out ? {5{1'b0}} : 5'bz;  // Controlled_Buffer controlled_buffer_106
  assign rd_t = and_43_out ? Juhis[11:7] : 5'bz;  // Controlled_Buffer controlled_buffer_107
  assign Data_type = and_43_out ? 3'b000 : 3'bz;  // Controlled_Buffer controlled_buffer_108
  assign ALU_src_B = and_43_out ? 1'b1 : 1'bz;  // Controlled_Buffer controlled_buffer_109
  assign Write_enable = and_43_out ? 1'b0 : 1'bz;  // Controlled_Buffer controlled_buffer_110
  assign CSR_write_enable = and_43_out ? 1'b0 : 1'bz;  // Controlled_Buffer controlled_buffer_111
  assign CSR_address = and_43_out ? {12{1'b0}} : 12'bz;  // Controlled_Buffer controlled_buffer_112
  assign PC_ctrl = and_43_out ? 3'b001 : 3'bz;  // Controlled_Buffer controlled_buffer_113
  assign Immidiate = and_44_out ? bit_extender_4_out : 32'bz;  // Controlled_Buffer controlled_buffer_114
  assign Command = and_44_out ? {5{1'b0}} : 5'bz;  // Controlled_Buffer controlled_buffer_115
  assign Register_mux = and_44_out ? 2'b00 : 2'bz;  // Controlled_Buffer controlled_buffer_116
  assign ALU_src_A = and_44_out ? 1'b1 : 1'bz;  // Controlled_Buffer controlled_buffer_117
  assign rs1 = and_44_out ? Juhis[19:15] : 5'bz;  // Controlled_Buffer controlled_buffer_118
  assign rs2 = and_44_out ? {5{1'b0}} : 5'bz;  // Controlled_Buffer controlled_buffer_119
  assign rd_t = and_44_out ? Juhis[11:7] : 5'bz;  // Controlled_Buffer controlled_buffer_120
  assign Data_type = and_44_out ? 3'b000 : 3'bz;  // Controlled_Buffer controlled_buffer_121
  assign ALU_src_B = and_44_out ? 1'b1 : 1'bz;  // Controlled_Buffer controlled_buffer_122
  assign Write_enable = and_44_out ? 1'b0 : 1'bz;  // Controlled_Buffer controlled_buffer_123
  assign CSR_write_enable = and_44_out ? 1'b0 : 1'bz;  // Controlled_Buffer controlled_buffer_124
  assign CSR_address = and_44_out ? {12{1'b0}} : 12'bz;  // Controlled_Buffer controlled_buffer_125
  assign PC_ctrl = and_44_out ? 3'b001 : 3'bz;  // Controlled_Buffer controlled_buffer_126
  assign mret = and_44_out ? 1'b0 : 1'bz;  // Controlled_Buffer controlled_buffer_127
  assign kehtiv = and_44_out ? 1'b1 : 1'bz;  // Controlled_Buffer controlled_buffer_128
  or or_37 (or_37_out, and_43_out, and_44_out);
  or or_38 (or_38_out, or_36_out, or_37_out);
  and and_45 (and_45_out, Juhis[0], Juhis[1], ~Juhis[2], ~Juhis[3], ~Juhis[4], Juhis[5], Juhis[6]);  // AND_Gate
  assign bit_extender_5_out = {{19{Juhis[31]}}, {Juhis[31], Juhis[7], Juhis[30:25], Juhis[11:8], 1'b0}};  // Bit_Extender bit_extender_5
  or or_39 (or_39_out, and_46_out, or_40_out);
  and and_46 (and_46_out, and_45_out, ~Juhis[12], ~Juhis[13], ~Juhis[14]);  // AND_Gate
  or or_40 (or_40_out, and_47_out, or_41_out);
  and and_47 (and_47_out, and_45_out, Juhis[12], ~Juhis[13], ~Juhis[14]);  // AND_Gate
  or or_41 (or_41_out, and_48_out, or_42_out);
  and and_48 (and_48_out, and_45_out, ~Juhis[12], ~Juhis[13], Juhis[14]);  // AND_Gate
  or or_42 (or_42_out, and_49_out, or_43_out);
  and and_49 (and_49_out, and_45_out, Juhis[12], ~Juhis[13], Juhis[14]);  // AND_Gate
  or or_43 (or_43_out, and_50_out, and_51_out);
  and and_50 (and_50_out, and_45_out, ~Juhis[12], Juhis[13], Juhis[14]);  // AND_Gate
  and and_51 (and_51_out, and_45_out, Juhis[12], Juhis[13], Juhis[14]);
  assign Immidiate = and_45_out ? bit_extender_5_out : 32'bz;  // Controlled_Buffer controlled_buffer_129
  assign Register_mux = and_45_out ? 2'b00 : 2'bz;  // Controlled_Buffer controlled_buffer_130
  assign ALU_src_A = and_45_out ? 1'b1 : 1'bz;  // Controlled_Buffer controlled_buffer_131
  assign rs1 = and_45_out ? Juhis[19:15] : 5'bz;  // Controlled_Buffer controlled_buffer_132
  assign rs2 = and_45_out ? Juhis[24:20] : 5'bz;  // Controlled_Buffer controlled_buffer_133
  assign rd_t = and_45_out ? {5{1'b0}} : 5'bz;  // Controlled_Buffer controlled_buffer_134
  assign Data_type = and_45_out ? 3'b000 : 3'bz;  // Controlled_Buffer controlled_buffer_135
  assign ALU_src_B = and_45_out ? 1'b0 : 1'bz;  // Controlled_Buffer controlled_buffer_136
  assign Write_enable = and_45_out ? 1'b0 : 1'bz;  // Controlled_Buffer controlled_buffer_137
  assign CSR_write_enable = and_45_out ? 1'b0 : 1'bz;  // Controlled_Buffer controlled_buffer_138
  assign CSR_address = and_45_out ? {12{1'b0}} : 12'bz;  // Controlled_Buffer controlled_buffer_139
  assign PC_ctrl = and_45_out ? 3'b100 : 3'bz;  // Controlled_Buffer controlled_buffer_140
  assign Branch_select = and_46_out ? 1'b1 : 1'bz;  // Controlled_Buffer controlled_buffer_141
  assign Command = and_46_out ? 5'b01001 : 5'bz;  // Controlled_Buffer controlled_buffer_142
  assign Branch_select = and_47_out ? 1'b0 : 1'bz;  // Controlled_Buffer controlled_buffer_143
  assign Command = and_47_out ? 5'b01001 : 5'bz;  // Controlled_Buffer controlled_buffer_144
  assign Branch_select = and_48_out ? 1'b0 : 1'bz;  // Controlled_Buffer controlled_buffer_145
  assign Command = and_48_out ? 5'b01001 : 5'bz;  // Controlled_Buffer controlled_buffer_146
  assign Branch_select = and_49_out ? 1'b1 : 1'bz;  // Controlled_Buffer controlled_buffer_147
  assign Command = and_49_out ? 5'b01001 : 5'bz;  // Controlled_Buffer controlled_buffer_148
  assign Branch_select = and_50_out ? 1'b0 : 1'bz;  // Controlled_Buffer controlled_buffer_149
  assign Command = and_50_out ? 5'b00010 : 5'bz;  // Controlled_Buffer controlled_buffer_150
  assign Branch_select = and_51_out ? 1'b1 : 1'bz;  // Controlled_Buffer controlled_buffer_151
  assign Command = and_51_out ? 5'b00010 : 5'bz;  // Controlled_Buffer controlled_buffer_152
  or or_44 (or_44_out, or_38_out, or_39_out);
  and and_52 (and_52_out, Juhis[0], Juhis[1], ~Juhis[2], ~Juhis[3], Juhis[4], Juhis[5], Juhis[6], ~Juhis[7], ~Juhis[8], ~Juhis[9], ~Juhis[10], ~Juhis[11], ~Juhis[12], ~Juhis[13], ~Juhis[14], ~Juhis[15], ~Juhis[17], ~Juhis[18], ~Juhis[19], Juhis[20], ~Juhis[21], Juhis[22], ~Juhis[23], ~Juhis[24], ~Juhis[25], ~Juhis[26], ~Juhis[27], Juhis[28], ~Juhis[29], ~Juhis[30], ~Juhis[31], ~Juhis[16]);  // AND_Gate
  and and_53 (erindid[1], Juhis[0], Juhis[1], ~Juhis[2], ~Juhis[3], Juhis[4], Juhis[5], Juhis[6], ~Juhis[7], ~Juhis[8], ~Juhis[9], ~Juhis[10], ~Juhis[11], ~Juhis[12], ~Juhis[13], ~Juhis[14], ~Juhis[15], ~Juhis[17], ~Juhis[18], ~Juhis[19], ~Juhis[20], ~Juhis[21], ~Juhis[22], ~Juhis[23], ~Juhis[24], ~Juhis[25], ~Juhis[26], ~Juhis[27], ~Juhis[28], ~Juhis[29], ~Juhis[30], ~Juhis[31], ~Juhis[16]);  // AND_Gate
  and and_54 (erindid[2], Juhis[0], Juhis[1], ~Juhis[2], ~Juhis[3], Juhis[4], Juhis[5], Juhis[6], ~Juhis[7], ~Juhis[8], ~Juhis[9], ~Juhis[10], ~Juhis[11], ~Juhis[12], ~Juhis[13], ~Juhis[14], ~Juhis[15], ~Juhis[17], ~Juhis[18], ~Juhis[19], Juhis[20], ~Juhis[21], ~Juhis[22], ~Juhis[23], ~Juhis[24], ~Juhis[25], ~Juhis[26], ~Juhis[27], ~Juhis[28], ~Juhis[29], ~Juhis[30], ~Juhis[31], ~Juhis[16]);  // AND_Gate
  and and_55 (mret, Juhis[0], Juhis[1], ~Juhis[2], ~Juhis[3], Juhis[4], Juhis[5], Juhis[6], ~Juhis[7], ~Juhis[8], ~Juhis[9], ~Juhis[10], ~Juhis[11], ~Juhis[12], ~Juhis[13], ~Juhis[14], ~Juhis[15], ~Juhis[17], ~Juhis[18], ~Juhis[19], ~Juhis[20], Juhis[21], ~Juhis[22], ~Juhis[23], ~Juhis[24], ~Juhis[25], ~Juhis[26], ~Juhis[27], Juhis[28], Juhis[29], ~Juhis[30], ~Juhis[31], ~Juhis[16]);  // AND_Gate
  or or_45 (or_45_out, or_46_out, and_52_out);
  or or_46 (or_46_out, or_47_out, erindid[1]);
  or or_47 (or_47_out, mret, erindid[2]);
  or or_48 (or_48_out, or_44_out, or_45_out);
  assign Immidiate = and_52_out ? {32{1'b0}} : 32'bz;  // Controlled_Buffer controlled_buffer_153
  assign Register_mux = and_52_out ? 2'b00 : 2'bz;  // Controlled_Buffer controlled_buffer_154
  assign ALU_src_A = and_52_out ? 1'b0 : 1'bz;  // Controlled_Buffer controlled_buffer_155
  assign rs1 = and_52_out ? {5{1'b0}} : 5'bz;  // Controlled_Buffer controlled_buffer_156
  assign rs2 = and_52_out ? {5{1'b0}} : 5'bz;  // Controlled_Buffer controlled_buffer_157
  assign rd_t = and_52_out ? {5{1'b0}} : 5'bz;  // Controlled_Buffer controlled_buffer_158
  assign Data_type = and_52_out ? 3'b000 : 3'bz;  // Controlled_Buffer controlled_buffer_159
  assign ALU_src_B = and_52_out ? 1'b1 : 1'bz;  // Controlled_Buffer controlled_buffer_160
  assign Write_enable = and_52_out ? 1'b0 : 1'bz;  // Controlled_Buffer controlled_buffer_161
  assign CSR_write_enable = and_52_out ? 1'b0 : 1'bz;  // Controlled_Buffer controlled_buffer_162
  assign CSR_address = and_52_out ? {12{1'b0}} : 12'bz;  // Controlled_Buffer controlled_buffer_163
  assign PC_ctrl = and_52_out ? 3'b010 : 3'bz;  // Controlled_Buffer controlled_buffer_164
  assign Branch_select = and_52_out ? 1'b0 : 1'bz;  // Controlled_Buffer controlled_buffer_165
  assign Command = and_52_out ? 5'b01001 : 5'bz;  // Controlled_Buffer controlled_buffer_166
  assign kehtiv = erindid[1] ? 1'b1 : 1'bz;  // Controlled_Buffer controlled_buffer_167
  assign Immidiate = erindid[1] ? {32{1'b0}} : 32'bz;  // Controlled_Buffer controlled_buffer_168
  assign Register_mux = erindid[1] ? 2'b00 : 2'bz;  // Controlled_Buffer controlled_buffer_169
  assign ALU_src_A = erindid[1] ? 1'b0 : 1'bz;  // Controlled_Buffer controlled_buffer_170
  assign rs1 = erindid[1] ? {5{1'b0}} : 5'bz;  // Controlled_Buffer controlled_buffer_171
  assign rs2 = erindid[1] ? {5{1'b0}} : 5'bz;  // Controlled_Buffer controlled_buffer_172
  assign rd_t = erindid[1] ? {5{1'b0}} : 5'bz;  // Controlled_Buffer controlled_buffer_173
  assign Data_type = erindid[1] ? 3'b000 : 3'bz;  // Controlled_Buffer controlled_buffer_174
  assign ALU_src_B = erindid[1] ? 1'b1 : 1'bz;  // Controlled_Buffer controlled_buffer_175
  assign Write_enable = erindid[1] ? 1'b0 : 1'bz;  // Controlled_Buffer controlled_buffer_176
  assign CSR_write_enable = erindid[1] ? 1'b0 : 1'bz;  // Controlled_Buffer controlled_buffer_177
  assign CSR_address = erindid[1] ? {12{1'b0}} : 12'bz;  // Controlled_Buffer controlled_buffer_178
  assign PC_ctrl = erindid[1] ? 3'b010 : 3'bz;  // Controlled_Buffer controlled_buffer_179
  assign Branch_select = erindid[1] ? 1'b0 : 1'bz;  // Controlled_Buffer controlled_buffer_180
  assign Command = erindid[1] ? 5'b01001 : 5'bz;  // Controlled_Buffer controlled_buffer_181
  assign Immidiate = erindid[2] ? {32{1'b0}} : 32'bz;  // Controlled_Buffer controlled_buffer_182
  assign Register_mux = erindid[2] ? 2'b00 : 2'bz;  // Controlled_Buffer controlled_buffer_183
  assign ALU_src_A = erindid[2] ? 1'b0 : 1'bz;  // Controlled_Buffer controlled_buffer_184
  assign rs1 = erindid[2] ? {5{1'b0}} : 5'bz;  // Controlled_Buffer controlled_buffer_185
  assign rs2 = erindid[2] ? {5{1'b0}} : 5'bz;  // Controlled_Buffer controlled_buffer_186
  assign rd_t = erindid[2] ? {5{1'b0}} : 5'bz;  // Controlled_Buffer controlled_buffer_187
  assign Data_type = erindid[2] ? 3'b000 : 3'bz;  // Controlled_Buffer controlled_buffer_188
  assign ALU_src_B = erindid[2] ? 1'b1 : 1'bz;  // Controlled_Buffer controlled_buffer_189
  assign Write_enable = erindid[2] ? 1'b0 : 1'bz;  // Controlled_Buffer controlled_buffer_190
  assign CSR_write_enable = erindid[2] ? 1'b0 : 1'bz;  // Controlled_Buffer controlled_buffer_191
  assign CSR_address = erindid[2] ? {12{1'b0}} : 12'bz;  // Controlled_Buffer controlled_buffer_192
  assign PC_ctrl = erindid[2] ? 3'b010 : 3'bz;  // Controlled_Buffer controlled_buffer_193
  assign Branch_select = erindid[2] ? 1'b0 : 1'bz;  // Controlled_Buffer controlled_buffer_194
  assign Command = erindid[2] ? 5'b01001 : 5'bz;  // Controlled_Buffer controlled_buffer_195
  assign mret = erindid[2] ? 1'b0 : 1'bz;  // Controlled_Buffer controlled_buffer_196
  assign kehtiv = mret ? 1'b1 : 1'bz;  // Controlled_Buffer controlled_buffer_197
  assign Immidiate = mret ? {32{1'b0}} : 32'bz;  // Controlled_Buffer controlled_buffer_198
  assign Register_mux = mret ? 2'b00 : 2'bz;  // Controlled_Buffer controlled_buffer_199
  assign ALU_src_A = mret ? 1'b0 : 1'bz;  // Controlled_Buffer controlled_buffer_200
  assign rs1 = mret ? {5{1'b0}} : 5'bz;  // Controlled_Buffer controlled_buffer_201
  assign rs2 = mret ? {5{1'b0}} : 5'bz;  // Controlled_Buffer controlled_buffer_202
  assign rd_t = mret ? {5{1'b0}} : 5'bz;  // Controlled_Buffer controlled_buffer_203
  assign Data_type = mret ? 3'b000 : 3'bz;  // Controlled_Buffer controlled_buffer_204
  assign ALU_src_B = mret ? 1'b1 : 1'bz;  // Controlled_Buffer controlled_buffer_205
  assign Write_enable = mret ? 1'b0 : 1'bz;  // Controlled_Buffer controlled_buffer_206
  assign CSR_write_enable = mret ? 1'b0 : 1'bz;  // Controlled_Buffer controlled_buffer_207
  assign CSR_address = mret ? {12{1'b0}} : 12'bz;  // Controlled_Buffer controlled_buffer_208
  assign PC_ctrl = mret ? 3'b010 : 3'bz;  // Controlled_Buffer controlled_buffer_209
  assign Branch_select = mret ? 1'b0 : 1'bz;  // Controlled_Buffer controlled_buffer_210
  assign Command = mret ? 5'b01001 : 5'bz;  // Controlled_Buffer controlled_buffer_211
  assign bit_extender_6_out = {{20{Juhis[31]}}, {Juhis[31:25], Juhis[11:7]}};  // Bit_Extender bit_extender_6
  and and_56 (and_56_out, Juhis[0], Juhis[1], ~Juhis[2], ~Juhis[3], ~Juhis[4], Juhis[5], ~Juhis[6]);  // AND_Gate
  and and_57 (and_57_out, and_56_out, ~Juhis[12], ~Juhis[13], ~Juhis[14]);  // AND_Gate
  and and_58 (and_58_out, and_56_out, Juhis[12], ~Juhis[13], ~Juhis[14]);  // AND_Gate
  and and_59 (and_59_out, and_56_out, ~Juhis[12], Juhis[13], ~Juhis[14]);  // AND_Gate
  assign Immidiate = and_56_out ? bit_extender_6_out : 32'bz;  // Controlled_Buffer controlled_buffer_212
  assign Register_mux = and_56_out ? 2'b00 : 2'bz;  // Controlled_Buffer controlled_buffer_213
  assign ALU_src_A = and_56_out ? 1'b1 : 1'bz;  // Controlled_Buffer controlled_buffer_214
  assign rs1 = and_56_out ? Juhis[19:15] : 5'bz;  // Controlled_Buffer controlled_buffer_215
  assign rs2 = and_56_out ? Juhis[24:20] : 5'bz;  // Controlled_Buffer controlled_buffer_216
  assign rd_t = and_56_out ? {5{1'b0}} : 5'bz;  // Controlled_Buffer controlled_buffer_217
  assign Command = and_56_out ? {5{1'b0}} : 5'bz;  // Controlled_Buffer controlled_buffer_218
  assign ALU_src_B = and_56_out ? 1'b1 : 1'bz;  // Controlled_Buffer controlled_buffer_219
  assign Write_enable = and_56_out ? 1'b1 : 1'bz;  // Controlled_Buffer controlled_buffer_220
  assign CSR_write_enable = and_56_out ? 1'b0 : 1'bz;  // Controlled_Buffer controlled_buffer_221
  assign CSR_address = and_56_out ? {12{1'b0}} : 12'bz;  // Controlled_Buffer controlled_buffer_222
  assign PC_ctrl = and_56_out ? 3'b000 : 3'bz;  // Controlled_Buffer controlled_buffer_223
  assign Branch_select = and_56_out ? 1'b0 : 1'bz;  // Controlled_Buffer controlled_buffer_224
  or or_49 (or_49_out, and_57_out, and_58_out, and_59_out);
  assign Data_type = and_57_out ? 3'b111 : 3'bz;  // Controlled_Buffer controlled_buffer_225
  assign Data_type = and_58_out ? 3'b110 : 3'bz;  // Controlled_Buffer controlled_buffer_226
  assign Data_type = and_59_out ? 3'b101 : 3'bz;  // Controlled_Buffer controlled_buffer_227
  or or_50 (or_50_out, or_48_out, or_49_out);
  assign bit_extender_7_out = {{20{Juhis[31]}}, Juhis[31:20]};  // Bit_Extender bit_extender_7
  and and_60 (and_60_out, Juhis[0], Juhis[1], ~Juhis[2], ~Juhis[3], ~Juhis[4], ~Juhis[5], ~Juhis[6]);  // AND_Gate
  or or_51 (or_51_out, or_52_out, and_61_out);
  and and_61 (and_61_out, and_60_out, ~Juhis[12], ~Juhis[13], ~Juhis[14]);  // AND_Gate
  or or_52 (or_52_out, and_62_out, or_53_out);
  and and_62 (and_62_out, and_60_out, Juhis[12], ~Juhis[13], ~Juhis[14]);  // AND_Gate
  or or_53 (or_53_out, or_54_out, and_63_out);
  and and_63 (and_63_out, and_60_out, ~Juhis[12], Juhis[13], ~Juhis[14]);  // AND_Gate
  or or_54 (or_54_out, and_64_out, and_65_out);
  and and_64 (and_64_out, and_60_out, ~Juhis[12], ~Juhis[13], Juhis[14]);  // AND_Gate
  and and_65 (and_65_out, and_60_out, Juhis[12], ~Juhis[13], Juhis[14]);  // AND_Gate
  assign Immidiate = and_60_out ? bit_extender_7_out : 32'bz;  // Controlled_Buffer controlled_buffer_228
  assign Register_mux = and_60_out ? 2'b11 : 2'bz;  // Controlled_Buffer controlled_buffer_229
  assign ALU_src_A = and_60_out ? 1'b1 : 1'bz;  // Controlled_Buffer controlled_buffer_230
  assign rs1 = and_60_out ? Juhis[19:15] : 5'bz;  // Controlled_Buffer controlled_buffer_231
  assign rs2 = and_60_out ? {5{1'b0}} : 5'bz;  // Controlled_Buffer controlled_buffer_232
  assign rd_t = and_60_out ? Juhis[11:7] : 5'bz;  // Controlled_Buffer controlled_buffer_233
  assign Command = and_60_out ? {5{1'b0}} : 5'bz;  // Controlled_Buffer controlled_buffer_234
  assign ALU_src_B = and_60_out ? 1'b1 : 1'bz;  // Controlled_Buffer controlled_buffer_235
  assign Write_enable = and_60_out ? 1'b0 : 1'bz;  // Controlled_Buffer controlled_buffer_236
  assign CSR_write_enable = and_60_out ? 1'b0 : 1'bz;  // Controlled_Buffer controlled_buffer_237
  assign CSR_address = and_60_out ? {12{1'b0}} : 12'bz;  // Controlled_Buffer controlled_buffer_238
  assign PC_ctrl = and_60_out ? 3'b000 : 3'bz;  // Controlled_Buffer controlled_buffer_239
  assign Branch_select = and_60_out ? 1'b1 : 1'bz;  // Controlled_Buffer controlled_buffer_240
  assign Data_type = and_61_out ? 3'b011 : 3'bz;  // Controlled_Buffer controlled_buffer_241
  assign Data_type = and_62_out ? 3'b001 : 3'bz;  // Controlled_Buffer controlled_buffer_242
  assign Data_type = and_63_out ? 3'b000 : 3'bz;  // Controlled_Buffer controlled_buffer_243
  assign Data_type = and_64_out ? 3'b100 : 3'bz;  // Controlled_Buffer controlled_buffer_244
  assign Data_type = and_65_out ? 3'b010 : 3'bz;  // Controlled_Buffer controlled_buffer_245
  or or_55 (kehtiv, or_50_out, or_51_out);
  not not_1 (erindid[0], kehtiv);
  Multiplexer #(.width(32)) multiplexer_1 (.in0({32{1'b0}}), .in1(Immidiate), .out(Otsene), .sel(kehtiv));
  Multiplexer #(.width(5)) multiplexer_2 (.in0({5{1'b0}}), .in1(Command), .out(Operatsioon), .sel(kehtiv));
  Multiplexer #(.width(2)) multiplexer_3 (.in0(2'b00), .in1(Register_mux), .out(Registri_mux), .sel(kehtiv));
  Multiplexer multiplexer_4 (.in0(1'b1), .in1(ALU_src_A), .out(ALU_sisend_A), .sel(kehtiv));
  Multiplexer #(.width(5)) multiplexer_5 (.in0({5{1'b0}}), .in1(rs1), .out(rsA), .sel(kehtiv));
  Multiplexer #(.width(5)) multiplexer_6 (.in0({5{1'b0}}), .in1(rs2), .out(rsB), .sel(kehtiv));
  Multiplexer #(.width(5)) multiplexer_7 (.in0({5{1'b0}}), .in1(rd_t), .out(rd), .sel(kehtiv));
  Multiplexer #(.width(3)) multiplexer_8 (.in0(3'b000), .in1(Data_type), .out(andmetuup), .sel(kehtiv));
  Multiplexer multiplexer_9 (.in0(1'b0), .in1(ALU_src_B), .out(ALU_sisend_B), .sel(kehtiv));
  Multiplexer multiplexer_10 (.in0(1'b0), .in1(Write_enable), .out(Luba_kirjutamine), .sel(kehtiv));
  Multiplexer multiplexer_11 (.in0(1'b0), .in1(CSR_write_enable), .out(CSR_luba_kirjutamine), .sel(kehtiv));
  Multiplexer #(.width(12)) multiplexer_12 (.in0({12{1'b0}}), .in1(CSR_address), .out(CSR_aadress), .sel(kehtiv));
  Multiplexer multiplexer_13 (.in0(1'b0), .in1(Branch_select), .out(Hargnemise_valik), .sel(kehtiv));
  Multiplexer #(.width(3)) multiplexer_14 (.in0(3'b010), .in1(PC_ctrl), .out(PC_kontroll), .sel(kehtiv));

  // Other names for the same wires on the sheet: ECALL = erindid[1]; EBREAK = erindid[2]

  // Notes on the sheet:
  //   Juhis: initial=0x1
  //   mret: pull=down
  //   erindid: pull=down
  //   ADD
  //   SUB
  //   AND
  //   OR
  //   XOR
  //   SLL
  //   SLT
  //   SLTU
  //   SRL
  //   SRA
  //   MUL
  //   MULH
  //   MULHU
  //   MULHSU
  //   DIVU
  //   REMU
  //   DIV
  //   REM
  //   R tüüpi
  //   LUI
  //   AUIPC
  //   U tüüpi
  //   ADDI
  //   SLTI
  //   SLTIU
  //   XORI
  //   ORI
  //   ANDI
  //   SLLI
  //   SRLI
  //   SRAI
  //   I type
  //   I type CSR
  //   CSRRW
  //   CSRRS
  //   CSRRC
  //   CSRRWI
  //   CSRRSI
  //   CSRRCI
  //   JAL
  //   JALR
  //   Jumps
  //   BEQ
  //   BNE
  //   BLT
  //   BGE
  //   BLTU
  //   BGEU
  //   B type (branch)
  //   WFI
  //   ECALL
  //   EBREAK
  //   MRET
  //   Store
  //   SB
  //   SH
  //   SW
  //   Malu kasud
  //   Load
  //   LB
  //   LH
  //   LW
  //   LBU
  //   LHU
endmodule

module Mikrokontroller (
);

  wire and_1_out, and_2_out, and_3_out, av1_output_1, av2_output_1, clock_1_out, CPU_1_kirjuta_mallu,
       nor_1_out, reset_out;
  wire [1:0] and_4_out, and_5_out, CPU_1_juhise_aadress, GPIO_p3_2, or_2_out, Timer_adv_1_viigu_kontroll,
       Timer_adv_1_viigud_valja;
  wire [2:2] or_1_out;
  wire [13:0] CPU_1_juhise_aadress_3;
  wire [15:0] CPU_1_juhise_aadress_2;
  wire [31:0] and_6_out, and_7_out, Andmed_q, Andmesuund_q, controlled_buffer_1_out, CPU_1_alu_valjund,
       CPU_1_malu_valjund, GPIO_p3, or_3_out, RAM_1_dout, ROM_1_data, Timer_adv_1_erandid;

  // Probe on CPU_1_juhise_aadress_2
  ROM #(.addrWidth(16), .dataWidth(32)) ROM_1 (.addr(CPU_1_juhise_aadress_2), .data(ROM_1_data));
  or or_1 (or_1_out[2], CPU_1_juhise_aadress_3[13], CPU_1_juhise_aadress_3[12], CPU_1_juhise_aadress_3[11], CPU_1_juhise_aadress_3[10], CPU_1_juhise_aadress_3[9], CPU_1_juhise_aadress_3[8], CPU_1_juhise_aadress_3[7], CPU_1_juhise_aadress_3[5], CPU_1_juhise_aadress_3[4], CPU_1_juhise_aadress_3[3], CPU_1_juhise_aadress_3[2], CPU_1_juhise_aadress_3[1], CPU_1_juhise_aadress_3[0], CPU_1_juhise_aadress_3[6]);
  Button reset (.out(reset_out));
  Clock clock_1 (.out(clock_1_out));
  CPU CPU_1 (
    .juhis(ROM_1_data), .malu_sisend(controlled_buffer_1_out), .reset(reset_out), .kell(clock_1_out),
    .katkestus(Timer_adv_1_erandid), .malu_viga({or_1_out[2], 2'b00}),
    .juhise_aadress({CPU_1_juhise_aadress_3, CPU_1_juhise_aadress_2, CPU_1_juhise_aadress}),
    .ALU_valjund(CPU_1_alu_valjund), .kirjuta_mallu(CPU_1_kirjuta_mallu), .malu_valjund(CPU_1_malu_valjund));
  and and_1 (and_1_out, CPU_1_kirjuta_mallu, nor_1_out);
  nor nor_1 (nor_1_out, ~CPU_1_alu_valjund[14], CPU_1_alu_valjund[15], CPU_1_alu_valjund[16], CPU_1_alu_valjund[17], CPU_1_alu_valjund[18], CPU_1_alu_valjund[19], CPU_1_alu_valjund[20], CPU_1_alu_valjund[21], CPU_1_alu_valjund[22], CPU_1_alu_valjund[24], CPU_1_alu_valjund[25], CPU_1_alu_valjund[26], CPU_1_alu_valjund[27], CPU_1_alu_valjund[28], CPU_1_alu_valjund[29], CPU_1_alu_valjund[30], CPU_1_alu_valjund[31], CPU_1_alu_valjund[23]);  // NOR_Gate
  // Probe on CPU_1_alu_valjund[13:2]
  RAM #(.addrWidth(12), .dataWidth(32), .enables("line")) RAM_1 (
    .addr(CPU_1_alu_valjund[13:2]), .we(and_1_out), .clk(clock_1_out), .din(CPU_1_malu_valjund),
    .dout(RAM_1_dout));
  assign controlled_buffer_1_out = nor_1_out ? RAM_1_dout : 32'bz;  // Controlled_Buffer controlled_buffer_1
  // Probe on CPU_1_alu_valjund
  Aadressi_vordleja av1 (.Input_bus_1(CPU_1_alu_valjund), .Input_bus_2({32{1'b0}}), .Output_1(av1_output_1));
  Aadressi_vordleja av2 (.Input_bus_1(CPU_1_alu_valjund), .Input_bus_2(32'h4), .Output_1(av2_output_1));
  // Probe on CPU_1_alu_valjund
  Register #(.width(32)) Andmed (.D(CPU_1_malu_valjund), .en(and_2_out), .clk(clock_1_out), .Q(Andmed_q));  // open: clr
  and and_2 (and_2_out, CPU_1_kirjuta_mallu, av1_output_1);
  Register #(.width(32)) Andmesuund (
    .D(CPU_1_malu_valjund), .en(and_3_out), .clk(clock_1_out), .Q(Andmesuund_q));  // open: clr
  and and_3 (and_3_out, CPU_1_kirjuta_mallu, av2_output_1);
  assign controlled_buffer_1_out = av2_output_1 ? Andmesuund_q : 32'bz;  // Controlled_Buffer controlled_buffer_2
  Taimer Timer_adv_1 (
    .Andmed_sisse(CPU_1_malu_valjund), .Malu_aadress(CPU_1_alu_valjund), .TMR_ADDR(32'h100),
    .Luba_kirjutamine(CPU_1_kirjuta_mallu), .Viigud_sisse(GPIO_p3_2), .CLK(clock_1_out),
    .Andmed_valja(controlled_buffer_1_out), .Erandid(Timer_adv_1_erandid[3:0]),
    .Viigud_valja(Timer_adv_1_viigud_valja), .Viigu_kontroll(Timer_adv_1_viigu_kontroll));
  assign and_4_out = ~Timer_adv_1_viigu_kontroll & Andmed_q[26:25];  // AND_Gate and_4, 2 bits wide
  // Probe on Timer_adv_1_viigud_valja
  assign and_5_out = Timer_adv_1_viigu_kontroll & Timer_adv_1_viigud_valja;  // AND_Gate and_5, 2 bits wide
  assign or_2_out = and_5_out | and_4_out;  // OR_Gate or_2, 2 bits wide
  assign controlled_buffer_1_out = av1_output_1 ? or_3_out : 32'bz;  // Controlled_Buffer controlled_buffer_3
  assign or_3_out = and_6_out | and_7_out;  // OR_Gate or_3, 32 bits wide
  assign and_6_out = Andmesuund_q & {Andmed_q[31:27], or_2_out, Andmed_q[24:0]};  // AND_Gate and_6, 32 bits wide
  // PortIO #(.direction("IOMultiEnable"), .number(32)) GPIO: pin names not known; wires that end beside it: Andmesuund_q, {Andmed_q[31:27], or_2_out, Andmed_q[24:0]}, {GPIO_p3[31:9], GPIO_p3_2, GPIO_p3[6:0]}
  assign and_7_out = ~Andmesuund_q & {GPIO_p3[31:9], GPIO_p3_2, GPIO_p3[6:0]};  // AND_Gate and_7, 32 bits wide
  Pull_Resistor pull_resistor_1 (.node({GPIO_p3[31:9], GPIO_p3_2, GPIO_p3[6:0]}));

  // Notes on the sheet:
  //   contents of ROM_1 (hex, n*v repeats v):
  //   1f90006f 2150006f 500293 300313 6283b3 752023 450513 fff00293 fff00313 6283b3 752023 450513 293 313
  //   6283b3 752023 450513 500293 300313 406283b3 752023 450513 fff00293 fff00313 406283b3 752023 450513
  //   100293 200313 406283b3 752023 450513 f0f0f2b7 f028293 ff010337 f0030313 62f3b3 752023 450513
  //   deadc2b7 eef28293 dadae337 ada30313 62f3b3 752023 450513 f0f0f2b7 f028293 ff010337 f0030313 62e3b3
  //   752023 450513 deadc2b7 eef28293 dadae337 ada30313 62e3b3 752023 450513 f0f0f2b7 f028293 ff010337
  //   f0030313 62c3b3 752023 450513 deadc2b7 eef28293 dadae337 ada30313 62c3b3 752023 450513 deadc2b7
  //   eef28293 deadc337 eef30313 62c3b3 752023 450513 ff2b7 100313 6293b3 752023 450513 100293 1f00313
  //   6293b3 752023 450513 800002b7 1f00313 62d3b3 752023 450513 ff2b7 100313 62d3b3 752023 450513
  //   fff00293 400313 4062d3b3 752023 450513 800002b7 1f00313 4062d3b3 752023 450513 500293 a00313 62a3b3
  //   752023 450513 a00293 500313 62a3b3 752023 450513 fff00293 313 62b3b3 752023 450513 293 fff00313
  //   62b3b3 752023 450513 500293 728393 752023 450513 500293 a2a393 752023 450513 293 c82b393 752023
  //   450513 aaaa52b7 55528293 ffff0337 62c3b3 752023 450513 100293 10337 f0030313 62e3b3 752023 450513
  //   123452b7 67828293 ff2f393 752023 450513 100293 a29393 752023 450513 800002b7 1f2d393 752023 450513
  //   fff00293 4012d393 752023 450513 123453b7 752023 450513 397 752023 450513 1000397 752023 450513
  //   500293 500313 26283b3 752023 450513 293 313 26283b3 752023 450513 182b7 6a028293 18337 6a030313
  //   26283b3 752023 450513 182b7 6a028293 18337 6a030313 26293b3 752023 450513 182b7 6a028293 fffe8337
  //   96030313 25323b3 752023 450513 fff00293 fff00313 262b3b3 752023 450513 fff00293 ffe00313 262b3b3
  //   752023 450513 400293 200313 262c3b3 752023 450513 400293 313 262c3b3 752023 450513 293 313 262c3b3
  //   752023 450513 400293 200313 262d3b3 752023 450513 400293 313 262d3b3 752023 450513 a00293 300313
  //   262e3b3 752023 450513 ff600293 300313 262e3b3 752023 450513 a00293 ffd00313 262e3b3 752023 450513
  //   ff600293 ffd00313 262e3b3 752023 450513 a00293 300313 262f3b3 752023 450513 ff600293 300313 262f3b3
  //   752023 450513 a00293 ffd00313 262f3b3 752023 450513 ff600293 ffd00313 262f3b3 752023 450513 8067
  //   100293 317 1030313 34131073 73 2e37 e2383 752023 450513 100293 317 1030313 34131073 100073 2e37
  //   e2383 752023 450513 a300393 752023 450513 1e4000ef 752023 450513 1100e13 1100e93 1de0863 13b7
  //   bad38393 80006f 5500393 752023 450513 2200e13 2200e93 1de1663 6600393 c0006f 13b7 bad38393 752023
  //   450513 ffb00e13 300e93 1de4863 13b7 bad38393 80006f 7100393 752023 450513 a00e13 500e93 1de4663
  //   7200393 c0006f 13b7 bad38393 752023 450513 700e13 300e93 1de5863 13b7 bad38393 80006f 8100393 752023
  //   450513 ff600e13 e93 1de5663 8200393 c0006f 13b7 bad38393 752023 450513 100e13 200e93 1de6863 13b7
  //   bad38393 80006f 9100393 752023 450513 ffe00e13 100e93 1de6663 9200393 c0006f 13b7 bad38393 752023
  //   450513 fff00e13 ffe00e93 1de7863 13b7 bad38393 80006f a100393 752023 450513 e13 100e93 1de7663
  //   a200393 c0006f 13b7 bad38393 752023 450513 12b7 23428293 317 3c830313 30531073 393 100e93 10039073
  //   10439073 10839073 108e9073 30402f73 2f6f13 304f1073 30002ff3 8fef93 300f9073 552023 450513 393
  //   10039073 ffd00e13 1cf7f33 304f1073 ff700e13 1cfffb3 300f9073 8067 4400393 e1dff06f 400313 ff00e13
  //   1c32023 313 aa00e13 1c32023 32e83 1d52023 450513 400313 e13 1c32023 313 5500e13 1c32023 32e83
  //   1d52023 450513 10000313 3900e13 1c32023 32e83 1d52023 450513 10400313 4d200e13 1c32023 32e83 1d52023
  //   450513 10800313 1e37 e1e0e13 1c32023 32e83 1d52023 450513 10c00313 2e37 70fe0e13 1c32023 32e83
  //   1d52023 450513 400313 ff00e13 1c32023 10000313 3900e13 1c32023 10400313 e13 1c32023 313 393 8000e13
  //   1c32023 732023 1c32023 732023 1c32023 732023 10400313 32e83 1d52023 450513 8067 30000313 300023f3
  //   fff00e13 300e1073 30002ef3 652023 752223 1c52423 1d52623 30039073 1050513 30100313 301023f3 a5a5ae37
  //   5a5e0e13 38e93 652023 752223 1c52423 1d52623 1050513 30400313 304023f3 aaaabe37 aaae0e13 304e1073
  //   30402ef3 652023 752223 1c52423 1d52623 30439073 1050513 30500313 305023f3 1e37 305e1073 30502ef3
  //   652023 7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
  //   0 - sisend
  //   1 - valjund
endmodule

module Aadressi_vordleja (
  input  [31:0] Input_bus_1,
  input  [31:0] Input_bus_2,
  output Output_1
);

  wire [31:0] xnor_1_out;

  assign xnor_1_out = ~(Input_bus_1 ^ Input_bus_2);  // XNOR_Gate xnor_1, 32 bits wide
  and and_1 (Output_1, xnor_1_out[16], xnor_1_out[2], xnor_1_out[3], xnor_1_out[4], xnor_1_out[5], xnor_1_out[6], xnor_1_out[7], xnor_1_out[8], xnor_1_out[9], xnor_1_out[10], xnor_1_out[11], xnor_1_out[12], xnor_1_out[13], xnor_1_out[14], xnor_1_out[15], xnor_1_out[17], xnor_1_out[18], xnor_1_out[19], xnor_1_out[20], xnor_1_out[21], xnor_1_out[22], xnor_1_out[23], xnor_1_out[24], xnor_1_out[25], xnor_1_out[26], xnor_1_out[27], xnor_1_out[28], xnor_1_out[29], xnor_1_out[30], xnor_1_out[31]);
endmodule

module Taimer (
  input  [31:0] Andmed_sisse,
  input  [31:0] Malu_aadress,
  input  [31:0] TMR_ADDR,
  input  Luba_kirjutamine,
  input  [1:0] Viigud_sisse,
  input  CLK,
  output [31:0] Andmed_valja,
  output [3:0] Erandid,
  output [1:0] Viigud_valja,
  output [1:0] Viigu_kontroll
);

  wire aadressi_vordleja_1_output_1, aadressi_vordleja_2_output_1, aadressi_vordleja_3_output_1,
       aadressi_vordleja_4_output_1, and_1_out, and_3_out, and_4_out, and_5_out, and_6_out, and_7_out,
       and_8_out, counter_1_carry, enkooder_1_kell_valja, enkooder_1_suund, multiplexer_2_out,
       multiplexer_3_out, multiplexer_4_out, multiplexer_5_out, not_2_out, or_2_out, or_3_out, or_4_out,
       or_5_out, undriven;
  wire [1:0] CNT_REG_q_2;
  wire [2:0] counter_1_q;
  wire [31:0] adder_1_out, adder_2_out, adder_3_out, and_2_out, CNT_REG_q, counter_2_q, multiplexer_1_out,
       or_1_out;
  wire [31:31] not_1_out;

  Adder #(.width(32)) adder_1 (.a(TMR_ADDR), .b(32'h4), .out(adder_1_out));  // open: cin, cout
  Adder #(.width(32)) adder_2 (.a(TMR_ADDR), .b(32'h8), .out(adder_2_out));  // open: cin, cout
  Adder #(.width(32)) adder_3 (.a(TMR_ADDR), .b(32'hc), .out(adder_3_out));  // open: cin, cout
  Aadressi_vordleja aadressi_vordleja_1 (
    .Input_bus_1(TMR_ADDR), .Input_bus_2(Malu_aadress), .Output_1(aadressi_vordleja_1_output_1));
  Aadressi_vordleja aadressi_vordleja_2 (
    .Input_bus_1(adder_1_out), .Input_bus_2(Malu_aadress), .Output_1(aadressi_vordleja_2_output_1));
  Aadressi_vordleja aadressi_vordleja_3 (
    .Input_bus_1(adder_2_out), .Input_bus_2(Malu_aadress), .Output_1(aadressi_vordleja_3_output_1));
  Aadressi_vordleja aadressi_vordleja_4 (
    .Input_bus_1(adder_3_out), .Input_bus_2(Malu_aadress), .Output_1(aadressi_vordleja_4_output_1));
  and and_1 (and_1_out, aadressi_vordleja_1_output_1, Luba_kirjutamine);
  Enkooder enkooder_1 (
    .A(Viigud_sisse[0]), .B(Viigud_sisse[1]), .Kell_sisse(CLK), .Suund(enkooder_1_suund),
    .Kell_valja(enkooder_1_kell_valja));
  assign or_1_out = {32{1'b0}} | {CNT_REG_q[31:15], Viigu_kontroll, CNT_REG_q[12:3], CNT_REG_q_2, CNT_REG_q[0]};  // OR_Gate or_1, 32 bits wide
  assign and_2_out = {not_1_out[31], {31{1'b1}}} & or_1_out;  // AND_Gate and_2, 32 bits wide
  Multiplexer #(.width(32)) multiplexer_1 (
    .in0(Andmed_sisse), .in1(and_2_out), .out(multiplexer_1_out), .sel(or_5_out));
  Register #(.width(32)) CNT_REG (
    .D(multiplexer_1_out), .en(and_1_out), .clk(CLK),
    .Q({CNT_REG_q[31:15], Viigu_kontroll, CNT_REG_q[12:3], CNT_REG_q_2, CNT_REG_q[0]}), .clr(undriven));
  not not_1 (not_1_out[31], or_5_out);
  assign Andmed_valja = aadressi_vordleja_1_output_1 ? {CNT_REG_q[31:15], Viigu_kontroll, CNT_REG_q[12:3], CNT_REG_q_2, CNT_REG_q[0]} : 32'bz;  // Controlled_Buffer controlled_buffer_1
  Multiplexer #(.select(2)) multiplexer_2 (
    .in0(CLK), .in1(enkooder_1_kell_valja), .in2(Viigud_sisse[0]), .in3(Viigud_sisse[1]),
    .out(multiplexer_2_out), .sel(CNT_REG_q[4:3]));
  Counter #(.max('h7), .width(3)) counter_1 (
    .clr(or_3_out), .load(1'b0), .up(1'b1), .clk(multiplexer_2_out), .carry(counter_1_carry), .Q(counter_1_q));  // open: count, D
  // Probe on {CNT_REG_q[31:15], Viigu_kontroll, CNT_REG_q[12:3], CNT_REG_q_2, CNT_REG_q[0]}
  and and_3 (and_3_out, Luba_kirjutamine, aadressi_vordleja_2_output_1);
  Vordlus_register CR0 (
    .taimeri_vaartus(counter_2_q), .andmesiin_sisse(Andmed_sisse), .WE(Luba_kirjutamine),
    .RS(aadressi_vordleja_3_output_1), .CLK(CLK), .andmesiin_valja(Andmed_valja), .kokkulangevus(Erandid[1]));
  Vordlus_register CR1 (
    .taimeri_vaartus(counter_2_q), .andmesiin_sisse(Andmed_sisse), .WE(Luba_kirjutamine),
    .RS(aadressi_vordleja_4_output_1), .CLK(CLK), .andmesiin_valja(Andmed_valja), .kokkulangevus(Erandid[2]));
  or or_2 (or_2_out, counter_1_carry, or_3_out);
  or or_3 (or_3_out, ~CNT_REG_q[0], multiplexer_3_out);  // OR_Gate
  Multiplexer #(.enable("true"), .select(2)) multiplexer_3 (
    .in0(counter_1_q[0]), .in1(counter_1_q[1]), .in2(counter_1_q[2]), .in3(1'b0), .out(multiplexer_3_out),
    .sel(CNT_REG_q_2), .en(CNT_REG_q[0]));
  not not_2 (not_2_out, CNT_REG_q[5]);
  Multiplexer multiplexer_4 (.in0(not_2_out), .in1(enkooder_1_suund), .out(multiplexer_4_out), .sel(CNT_REG_q[12]));
  Multiplexer multiplexer_5 (.in0(or_2_out), .in1(CLK), .out(multiplexer_5_out), .sel(and_3_out));
  and and_4 (and_4_out, CNT_REG_q[6], Erandid[1]);
  or or_4 (or_4_out, and_4_out, and_5_out);
  and and_5 (and_5_out, CNT_REG_q[7], Erandid[2]);
  assign Andmed_valja = aadressi_vordleja_2_output_1 ? counter_2_q : 32'bz;  // Controlled_Buffer controlled_buffer_2
  Counter #(.max('hffffffff), .width(32)) counter_2 (
    .load(and_3_out), .D(Andmed_sisse), .count(CNT_REG_q[0]), .Q(counter_2_q), .carry(Erandid[0]),
    .up(multiplexer_4_out), .clk(multiplexer_5_out), .clr(or_4_out));
  or or_5 (or_5_out, and_8_out, and_7_out, and_6_out);
  and and_6 (and_6_out, CNT_REG_q[10], Erandid[0]);
  and and_7 (and_7_out, CNT_REG_q[8], Erandid[1]);
  and and_8 (and_8_out, CNT_REG_q[9], Erandid[2]);
  S_R_Flip_Flop #(.trigger("low")) s_r_ff_1 (
    .S(Erandid[1]), .R(or_4_out), .clk(1'b0), .Q(Viigud_valja[0]));  // open: reset, Qn, preset
  S_R_Flip_Flop #(.trigger("low")) s_r_ff_2 (
    .S(Erandid[2]), .R(or_4_out), .clk(1'b0), .Q(Viigud_valja[1]));  // open: reset, Qn, preset

  // Notes on the sheet:
  //   CR - Kontrollregister
  //   0 - käivita
  //   5 - üles_alla
  //   [8-10] - üksik
  //   [1,2] - kella jagaja
  //   [3,4] - kella sisend
  //   [6,7] - CR_lähtestus
  //   12 - enkoodri suuna valik
  //   [13-14] - väljundviigu kontroll
endmodule

module Vordlus_register (
  input  [31:0] taimeri_vaartus,
  input  [31:0] andmesiin_sisse,
  input  WE,
  input  RS,
  input  CLK,
  output kokkulangevus,
  output [31:0] andmesiin_valja
);

  wire and_1_out;
  wire [31:0] register_1_q;

  and and_1 (and_1_out, WE, RS);
  Register #(.width(32)) register_1 (.D(andmesiin_sisse), .en(and_1_out), .clk(CLK), .Q(register_1_q));  // open: clr
  assign andmesiin_valja = RS ? register_1_q : 32'bz;  // Controlled_Buffer controlled_buffer_1
  Comparator #(.mode("unsigned"), .width(32)) comparator_1 (
    .a(taimeri_vaartus), .b(register_1_q), .eq(kokkulangevus));  // open: gt, lt
endmodule

module Enkooder (
  input  A,
  input  B,
  input  Kell_sisse,
  output Suund,
  output Kell_valja
);

  wire and_1_out, and_2_out, and_3_out, and_4_out, and_5_out, and_6_out, and_7_out, and_8_out, d_ff_1_q,
       d_ff_2_q, Eelmine_A_q, Eelmine_B_q, or_2_out, or_3_out;

  D_Flip_Flop d_ff_1 (.D(A), .clk(Kell_sisse), .Q(d_ff_1_q));  // open: Qn, preset, reset
  D_Flip_Flop d_ff_2 (.D(B), .clk(Kell_sisse), .Q(d_ff_2_q));  // open: Qn, preset, reset
  D_Flip_Flop Eelmine_A (.D(d_ff_1_q), .clk(Kell_sisse), .Q(Eelmine_A_q));  // open: Qn, preset, reset
  D_Flip_Flop Eelmine_B (.D(d_ff_2_q), .clk(Kell_sisse), .Q(Eelmine_B_q));  // open: Qn, preset, reset
  and and_1 (and_1_out, d_ff_1_q, ~d_ff_2_q, ~Eelmine_A_q, ~Eelmine_B_q);  // AND_Gate
  and and_2 (and_2_out, d_ff_1_q, d_ff_2_q, Eelmine_A_q, ~Eelmine_B_q);  // AND_Gate
  and and_3 (and_3_out, ~d_ff_1_q, d_ff_2_q, Eelmine_A_q, Eelmine_B_q);  // AND_Gate
  and and_4 (and_4_out, ~d_ff_1_q, ~d_ff_2_q, ~Eelmine_A_q, Eelmine_B_q);  // AND_Gate
  and and_5 (and_5_out, ~d_ff_1_q, d_ff_2_q, ~Eelmine_A_q, ~Eelmine_B_q);  // AND_Gate
  and and_6 (and_6_out, d_ff_1_q, d_ff_2_q, ~Eelmine_A_q, Eelmine_B_q);  // AND_Gate
  and and_7 (and_7_out, d_ff_1_q, ~d_ff_2_q, Eelmine_A_q, Eelmine_B_q);  // AND_Gate
  and and_8 (and_8_out, ~d_ff_1_q, ~d_ff_2_q, Eelmine_A_q, ~Eelmine_B_q);  // AND_Gate
  or or_1 (Suund, and_1_out, and_2_out, and_3_out, and_4_out);
  or or_2 (or_2_out, and_5_out, and_6_out, and_7_out, and_8_out);
  or or_3 (or_3_out, Suund, or_2_out);
  and and_9 (Kell_valja, or_3_out, ~Kell_sisse);  // AND_Gate
endmodule
module Korrutaja (
  input  a_mark,
  input  [31:0] a,
  input  b_mark,
  input  [31:0] b,
  output [31:0] result,
  output [31:0] carry
);

  wire adder_3_cout, adder_4_cout, adder_5_cout, adder_6_cout, adder_7_cout, adder_8_cout, adder_9_cout,
       adder_10_cout, adder_11_cout, adder_12_cout, adder_13_cout, adder_14_cout, adder_15_cout,
       adder_16_cout, adder_17_cout, adder_18_cout, adder_19_cout, adder_20_cout, adder_21_cout,
       adder_22_cout, adder_23_cout, adder_24_cout, adder_25_cout, adder_26_cout, adder_27_cout,
       adder_28_cout, adder_29_cout, adder_30_cout, adder_31_cout, adder_32_cout, and_1_out, and_2_out,
       and_3_out, and_4_out, xor_1_out;
  wire [63:0] adder_1_out, adder_2_out, adder_3_out, adder_4_out, adder_5_out, adder_6_out, adder_7_out,
       adder_8_out, adder_9_out, adder_10_out, adder_11_out, adder_12_out, adder_13_out, adder_14_out,
       adder_15_out, adder_16_out, adder_17_out, adder_18_out, adder_19_out, adder_20_out, adder_21_out,
       adder_22_out, adder_23_out, adder_24_out, adder_25_out, adder_26_out, adder_27_out, adder_28_out,
       adder_29_out, adder_30_out, adder_31_out, adder_32_out, adder_33_out, adder_34_out, and_5_out,
       and_6_out, and_7_out, and_8_out, and_9_out, and_10_out, and_11_out, and_12_out, and_13_out,
       and_14_out, and_15_out, and_16_out, and_17_out, and_18_out, and_19_out, and_20_out, and_21_out,
       and_22_out, and_23_out, and_24_out, and_25_out, and_26_out, and_27_out, and_28_out, and_29_out,
       and_30_out, and_31_out, and_32_out, and_33_out, and_34_out, and_35_out, and_36_out,
       bit_extender_1_out, bit_extender_2_out, bit_extender_3_out, bit_extender_4_out, bit_extender_5_out,
       bit_extender_6_out, bit_extender_7_out, bit_extender_8_out, bit_extender_9_out, bit_extender_10_out,
       bit_extender_11_out, bit_extender_12_out, bit_extender_13_out, bit_extender_14_out,
       bit_extender_15_out, bit_extender_16_out, bit_extender_17_out, bit_extender_18_out,
       bit_extender_19_out, bit_extender_20_out, bit_extender_21_out, bit_extender_22_out,
       bit_extender_23_out, bit_extender_24_out, bit_extender_25_out, bit_extender_26_out,
       bit_extender_27_out, bit_extender_28_out, bit_extender_29_out, bit_extender_30_out,
       bit_extender_31_out, bit_extender_32_out, bit_extender_33_out, bit_extender_34_out, multiplexer_1_out,
       multiplexer_2_out, not_1_out, not_2_out, not_3_out, shifter_1_out, shifter_2_out, shifter_3_out,
       shifter_4_out, shifter_5_out, shifter_6_out, shifter_7_out, shifter_8_out, shifter_9_out,
       shifter_10_out, shifter_11_out, shifter_12_out, shifter_13_out, shifter_14_out, shifter_15_out,
       shifter_16_out, shifter_17_out, shifter_18_out, shifter_19_out, shifter_20_out, shifter_21_out,
       shifter_22_out, shifter_23_out, shifter_24_out, shifter_25_out, shifter_26_out, shifter_27_out,
       shifter_28_out, shifter_29_out, shifter_30_out, shifter_31_out;

  and and_1 (and_1_out, a_mark, a[31]);
  and and_2 (and_2_out, b_mark, b[31]);
  assign bit_extender_1_out = {{32{and_1_out}}, a};  // Bit_Extender bit_extender_1
  assign bit_extender_2_out = {{32{and_2_out}}, b};  // Bit_Extender bit_extender_2
  assign not_1_out = ~bit_extender_1_out;  // NOT_Gate not_1, 64 bits wide
  assign not_2_out = ~bit_extender_2_out;  // NOT_Gate not_2, 64 bits wide
  Adder #(.width(64)) adder_1 (.a(not_1_out), .b(64'h1), .out(adder_1_out));  // open: cin, cout
  Adder #(.width(64)) adder_2 (.a(not_2_out), .b(64'h1), .out(adder_2_out));  // open: cin, cout
  and and_3 (and_3_out, a_mark, bit_extender_1_out[63]);
  Multiplexer #(.width(64)) multiplexer_1 (
    .in0(bit_extender_1_out), .in1(adder_1_out), .out(multiplexer_1_out), .sel(and_3_out));
  and and_4 (and_4_out, b_mark, bit_extender_2_out[63]);
  Multiplexer #(.width(64)) multiplexer_2 (
    .in0(bit_extender_2_out), .in1(adder_2_out), .out(multiplexer_2_out), .sel(and_4_out));
  xor xor_1 (xor_1_out, and_3_out, and_4_out);
  Shifter #(.width(64)) shifter_1 (.in(multiplexer_1_out), .\dist (6'b000001), .out(shifter_1_out));
  Shifter #(.width(64)) shifter_2 (.in(multiplexer_1_out), .\dist (6'b000010), .out(shifter_2_out));
  Shifter #(.width(64)) shifter_3 (.in(multiplexer_1_out), .\dist (6'b000011), .out(shifter_3_out));
  Shifter #(.width(64)) shifter_4 (.in(multiplexer_1_out), .\dist (6'b000100), .out(shifter_4_out));
  Shifter #(.width(64)) shifter_5 (.in(multiplexer_1_out), .\dist (6'b000101), .out(shifter_5_out));
  Shifter #(.width(64)) shifter_6 (.in(multiplexer_1_out), .\dist (6'b000110), .out(shifter_6_out));
  Shifter #(.width(64)) shifter_7 (.in(multiplexer_1_out), .\dist (6'b000111), .out(shifter_7_out));
  Shifter #(.width(64)) shifter_8 (.in(multiplexer_1_out), .\dist (6'b001000), .out(shifter_8_out));
  Shifter #(.width(64)) shifter_9 (.in(multiplexer_1_out), .\dist (6'b001001), .out(shifter_9_out));
  Shifter #(.width(64)) shifter_10 (.in(multiplexer_1_out), .\dist (6'b001010), .out(shifter_10_out));
  Shifter #(.width(64)) shifter_11 (.in(multiplexer_1_out), .\dist (6'b001011), .out(shifter_11_out));
  Shifter #(.width(64)) shifter_12 (.in(multiplexer_1_out), .\dist (6'b001100), .out(shifter_12_out));
  Shifter #(.width(64)) shifter_13 (.in(multiplexer_1_out), .\dist (6'b001101), .out(shifter_13_out));
  Shifter #(.width(64)) shifter_14 (.in(multiplexer_1_out), .\dist (6'b001110), .out(shifter_14_out));
  Shifter #(.width(64)) shifter_15 (.in(multiplexer_1_out), .\dist (6'b001111), .out(shifter_15_out));
  Shifter #(.width(64)) shifter_16 (.in(multiplexer_1_out), .\dist (6'b010000), .out(shifter_16_out));
  Shifter #(.width(64)) shifter_17 (.in(multiplexer_1_out), .\dist (6'b010001), .out(shifter_17_out));
  Shifter #(.width(64)) shifter_18 (.in(multiplexer_1_out), .\dist (6'b010010), .out(shifter_18_out));
  Shifter #(.width(64)) shifter_19 (.in(multiplexer_1_out), .\dist (6'b010011), .out(shifter_19_out));
  Shifter #(.width(64)) shifter_20 (.in(multiplexer_1_out), .\dist (6'b010100), .out(shifter_20_out));
  Shifter #(.width(64)) shifter_21 (.in(multiplexer_1_out), .\dist (6'b010101), .out(shifter_21_out));
  Shifter #(.width(64)) shifter_22 (.in(multiplexer_1_out), .\dist (6'b010110), .out(shifter_22_out));
  Shifter #(.width(64)) shifter_23 (.in(multiplexer_1_out), .\dist (6'b010111), .out(shifter_23_out));
  Shifter #(.width(64)) shifter_24 (.in(multiplexer_1_out), .\dist (6'b011000), .out(shifter_24_out));
  Shifter #(.width(64)) shifter_25 (.in(multiplexer_1_out), .\dist (6'b011001), .out(shifter_25_out));
  Shifter #(.width(64)) shifter_26 (.in(multiplexer_1_out), .\dist (6'b011010), .out(shifter_26_out));
  Shifter #(.width(64)) shifter_27 (.in(multiplexer_1_out), .\dist (6'b011011), .out(shifter_27_out));
  Shifter #(.width(64)) shifter_28 (.in(multiplexer_1_out), .\dist (6'b011100), .out(shifter_28_out));
  Shifter #(.width(64)) shifter_29 (.in(multiplexer_1_out), .\dist (6'b011101), .out(shifter_29_out));
  Shifter #(.width(64)) shifter_30 (.in(multiplexer_1_out), .\dist (6'b011110), .out(shifter_30_out));
  Shifter #(.width(64)) shifter_31 (.in(multiplexer_1_out), .\dist (6'b011111), .out(shifter_31_out));
  assign bit_extender_3_out = {{63{multiplexer_2_out[0]}}, multiplexer_2_out[0]};  // Bit_Extender bit_extender_3
  assign bit_extender_4_out = {{63{multiplexer_2_out[1]}}, multiplexer_2_out[1]};  // Bit_Extender bit_extender_4
  assign bit_extender_5_out = {{63{multiplexer_2_out[2]}}, multiplexer_2_out[2]};  // Bit_Extender bit_extender_5
  assign bit_extender_6_out = {{63{multiplexer_2_out[3]}}, multiplexer_2_out[3]};  // Bit_Extender bit_extender_6
  assign bit_extender_7_out = {{63{multiplexer_2_out[4]}}, multiplexer_2_out[4]};  // Bit_Extender bit_extender_7
  assign bit_extender_8_out = {{63{multiplexer_2_out[5]}}, multiplexer_2_out[5]};  // Bit_Extender bit_extender_8
  assign bit_extender_9_out = {{63{multiplexer_2_out[6]}}, multiplexer_2_out[6]};  // Bit_Extender bit_extender_9
  assign bit_extender_10_out = {{63{multiplexer_2_out[7]}}, multiplexer_2_out[7]};  // Bit_Extender bit_extender_10
  assign bit_extender_11_out = {{63{multiplexer_2_out[8]}}, multiplexer_2_out[8]};  // Bit_Extender bit_extender_11
  assign bit_extender_12_out = {{63{multiplexer_2_out[9]}}, multiplexer_2_out[9]};  // Bit_Extender bit_extender_12
  assign bit_extender_13_out = {{63{multiplexer_2_out[10]}}, multiplexer_2_out[10]};  // Bit_Extender bit_extender_13
  assign bit_extender_14_out = {{63{multiplexer_2_out[11]}}, multiplexer_2_out[11]};  // Bit_Extender bit_extender_14
  assign bit_extender_15_out = {{63{multiplexer_2_out[12]}}, multiplexer_2_out[12]};  // Bit_Extender bit_extender_15
  assign bit_extender_16_out = {{63{multiplexer_2_out[13]}}, multiplexer_2_out[13]};  // Bit_Extender bit_extender_16
  assign bit_extender_17_out = {{63{multiplexer_2_out[14]}}, multiplexer_2_out[14]};  // Bit_Extender bit_extender_17
  assign bit_extender_18_out = {{63{multiplexer_2_out[15]}}, multiplexer_2_out[15]};  // Bit_Extender bit_extender_18
  assign bit_extender_19_out = {{63{multiplexer_2_out[16]}}, multiplexer_2_out[16]};  // Bit_Extender bit_extender_19
  assign bit_extender_20_out = {{63{multiplexer_2_out[17]}}, multiplexer_2_out[17]};  // Bit_Extender bit_extender_20
  assign bit_extender_21_out = {{63{multiplexer_2_out[18]}}, multiplexer_2_out[18]};  // Bit_Extender bit_extender_21
  assign bit_extender_22_out = {{63{multiplexer_2_out[19]}}, multiplexer_2_out[19]};  // Bit_Extender bit_extender_22
  assign bit_extender_23_out = {{63{multiplexer_2_out[20]}}, multiplexer_2_out[20]};  // Bit_Extender bit_extender_23
  assign bit_extender_24_out = {{63{multiplexer_2_out[21]}}, multiplexer_2_out[21]};  // Bit_Extender bit_extender_24
  assign bit_extender_25_out = {{63{multiplexer_2_out[22]}}, multiplexer_2_out[22]};  // Bit_Extender bit_extender_25
  assign bit_extender_26_out = {{63{multiplexer_2_out[23]}}, multiplexer_2_out[23]};  // Bit_Extender bit_extender_26
  assign bit_extender_27_out = {{63{multiplexer_2_out[24]}}, multiplexer_2_out[24]};  // Bit_Extender bit_extender_27
  assign bit_extender_28_out = {{63{multiplexer_2_out[25]}}, multiplexer_2_out[25]};  // Bit_Extender bit_extender_28
  assign bit_extender_29_out = {{63{multiplexer_2_out[26]}}, multiplexer_2_out[26]};  // Bit_Extender bit_extender_29
  assign bit_extender_30_out = {{63{multiplexer_2_out[27]}}, multiplexer_2_out[27]};  // Bit_Extender bit_extender_30
  assign bit_extender_31_out = {{63{multiplexer_2_out[28]}}, multiplexer_2_out[28]};  // Bit_Extender bit_extender_31
  assign bit_extender_32_out = {{63{multiplexer_2_out[29]}}, multiplexer_2_out[29]};  // Bit_Extender bit_extender_32
  assign bit_extender_33_out = {{63{multiplexer_2_out[30]}}, multiplexer_2_out[30]};  // Bit_Extender bit_extender_33
  assign bit_extender_34_out = {{63{multiplexer_2_out[31]}}, multiplexer_2_out[31]};  // Bit_Extender bit_extender_34
  assign and_5_out = bit_extender_3_out & multiplexer_1_out;  // AND_Gate and_5, 64 bits wide
  assign and_6_out = bit_extender_4_out & shifter_1_out;  // AND_Gate and_6, 64 bits wide
  assign and_7_out = bit_extender_5_out & shifter_2_out;  // AND_Gate and_7, 64 bits wide
  assign and_8_out = bit_extender_6_out & shifter_3_out;  // AND_Gate and_8, 64 bits wide
  assign and_9_out = bit_extender_7_out & shifter_4_out;  // AND_Gate and_9, 64 bits wide
  assign and_10_out = bit_extender_8_out & shifter_5_out;  // AND_Gate and_10, 64 bits wide
  assign and_11_out = bit_extender_9_out & shifter_6_out;  // AND_Gate and_11, 64 bits wide
  assign and_12_out = bit_extender_10_out & shifter_7_out;  // AND_Gate and_12, 64 bits wide
  assign and_13_out = bit_extender_11_out & shifter_8_out;  // AND_Gate and_13, 64 bits wide
  assign and_14_out = bit_extender_12_out & shifter_9_out;  // AND_Gate and_14, 64 bits wide
  assign and_15_out = bit_extender_13_out & shifter_10_out;  // AND_Gate and_15, 64 bits wide
  assign and_16_out = bit_extender_14_out & shifter_11_out;  // AND_Gate and_16, 64 bits wide
  assign and_17_out = bit_extender_15_out & shifter_12_out;  // AND_Gate and_17, 64 bits wide
  assign and_18_out = bit_extender_16_out & shifter_13_out;  // AND_Gate and_18, 64 bits wide
  assign and_19_out = bit_extender_17_out & shifter_14_out;  // AND_Gate and_19, 64 bits wide
  assign and_20_out = bit_extender_18_out & shifter_15_out;  // AND_Gate and_20, 64 bits wide
  assign and_21_out = bit_extender_19_out & shifter_16_out;  // AND_Gate and_21, 64 bits wide
  assign and_22_out = bit_extender_20_out & shifter_17_out;  // AND_Gate and_22, 64 bits wide
  assign and_23_out = bit_extender_21_out & shifter_18_out;  // AND_Gate and_23, 64 bits wide
  assign and_24_out = bit_extender_22_out & shifter_19_out;  // AND_Gate and_24, 64 bits wide
  assign and_25_out = bit_extender_23_out & shifter_20_out;  // AND_Gate and_25, 64 bits wide
  assign and_26_out = bit_extender_24_out & shifter_21_out;  // AND_Gate and_26, 64 bits wide
  assign and_27_out = bit_extender_25_out & shifter_22_out;  // AND_Gate and_27, 64 bits wide
  assign and_28_out = bit_extender_26_out & shifter_23_out;  // AND_Gate and_28, 64 bits wide
  assign and_29_out = bit_extender_27_out & shifter_24_out;  // AND_Gate and_29, 64 bits wide
  assign and_30_out = bit_extender_28_out & shifter_25_out;  // AND_Gate and_30, 64 bits wide
  assign and_31_out = bit_extender_29_out & shifter_26_out;  // AND_Gate and_31, 64 bits wide
  assign and_32_out = bit_extender_30_out & shifter_27_out;  // AND_Gate and_32, 64 bits wide
  assign and_33_out = bit_extender_31_out & shifter_28_out;  // AND_Gate and_33, 64 bits wide
  assign and_34_out = bit_extender_32_out & shifter_29_out;  // AND_Gate and_34, 64 bits wide
  assign and_35_out = bit_extender_33_out & shifter_30_out;  // AND_Gate and_35, 64 bits wide
  assign and_36_out = bit_extender_34_out & shifter_31_out;  // AND_Gate and_36, 64 bits wide
  Adder #(.width(64)) adder_3 (.a(and_5_out), .b(and_6_out), .out(adder_3_out), .cout(adder_3_cout));  // open: cin
  Adder #(.width(64)) adder_4 (
    .a(adder_3_out), .b(and_7_out), .out(adder_4_out), .cin(adder_3_cout), .cout(adder_4_cout));
  Adder #(.width(64)) adder_5 (
    .a(adder_4_out), .b(and_8_out), .out(adder_5_out), .cin(adder_4_cout), .cout(adder_5_cout));
  Adder #(.width(64)) adder_6 (
    .a(adder_5_out), .b(and_9_out), .out(adder_6_out), .cin(adder_5_cout), .cout(adder_6_cout));
  Adder #(.width(64)) adder_7 (
    .a(adder_6_out), .b(and_10_out), .out(adder_7_out), .cin(adder_6_cout), .cout(adder_7_cout));
  Adder #(.width(64)) adder_8 (
    .a(adder_7_out), .b(and_11_out), .out(adder_8_out), .cin(adder_7_cout), .cout(adder_8_cout));
  Adder #(.width(64)) adder_9 (
    .a(adder_8_out), .b(and_12_out), .out(adder_9_out), .cin(adder_8_cout), .cout(adder_9_cout));
  Adder #(.width(64)) adder_10 (
    .a(adder_9_out), .b(and_13_out), .out(adder_10_out), .cin(adder_9_cout), .cout(adder_10_cout));
  Adder #(.width(64)) adder_11 (
    .a(adder_10_out), .b(and_14_out), .out(adder_11_out), .cin(adder_10_cout), .cout(adder_11_cout));
  Adder #(.width(64)) adder_12 (
    .a(adder_11_out), .b(and_15_out), .out(adder_12_out), .cin(adder_11_cout), .cout(adder_12_cout));
  Adder #(.width(64)) adder_13 (
    .a(adder_12_out), .b(and_16_out), .out(adder_13_out), .cin(adder_12_cout), .cout(adder_13_cout));
  Adder #(.width(64)) adder_14 (
    .a(adder_13_out), .b(and_17_out), .out(adder_14_out), .cin(adder_13_cout), .cout(adder_14_cout));
  Adder #(.width(64)) adder_15 (
    .a(adder_14_out), .b(and_18_out), .out(adder_15_out), .cin(adder_14_cout), .cout(adder_15_cout));
  Adder #(.width(64)) adder_16 (
    .a(adder_15_out), .b(and_19_out), .out(adder_16_out), .cin(adder_15_cout), .cout(adder_16_cout));
  Adder #(.width(64)) adder_17 (
    .a(adder_16_out), .b(and_20_out), .out(adder_17_out), .cin(adder_16_cout), .cout(adder_17_cout));
  Adder #(.width(64)) adder_18 (
    .a(adder_17_out), .b(and_21_out), .out(adder_18_out), .cin(adder_17_cout), .cout(adder_18_cout));
  Adder #(.width(64)) adder_19 (
    .a(adder_18_out), .b(and_22_out), .out(adder_19_out), .cin(adder_18_cout), .cout(adder_19_cout));
  Adder #(.width(64)) adder_20 (
    .a(adder_19_out), .b(and_23_out), .out(adder_20_out), .cin(adder_19_cout), .cout(adder_20_cout));
  Adder #(.width(64)) adder_21 (
    .a(adder_20_out), .b(and_24_out), .out(adder_21_out), .cin(adder_20_cout), .cout(adder_21_cout));
  Adder #(.width(64)) adder_22 (
    .a(adder_21_out), .b(and_25_out), .out(adder_22_out), .cin(adder_21_cout), .cout(adder_22_cout));
  Adder #(.width(64)) adder_23 (
    .a(adder_22_out), .b(and_26_out), .out(adder_23_out), .cin(adder_22_cout), .cout(adder_23_cout));
  Adder #(.width(64)) adder_24 (
    .a(adder_23_out), .b(and_27_out), .out(adder_24_out), .cin(adder_23_cout), .cout(adder_24_cout));
  Adder #(.width(64)) adder_25 (
    .a(adder_24_out), .b(and_28_out), .out(adder_25_out), .cin(adder_24_cout), .cout(adder_25_cout));
  Adder #(.width(64)) adder_26 (
    .a(adder_25_out), .b(and_29_out), .out(adder_26_out), .cin(adder_25_cout), .cout(adder_26_cout));
  Adder #(.width(64)) adder_27 (
    .a(adder_26_out), .b(and_30_out), .out(adder_27_out), .cin(adder_26_cout), .cout(adder_27_cout));
  Adder #(.width(64)) adder_28 (
    .a(adder_27_out), .b(and_31_out), .out(adder_28_out), .cin(adder_27_cout), .cout(adder_28_cout));
  Adder #(.width(64)) adder_29 (
    .a(adder_28_out), .b(and_32_out), .out(adder_29_out), .cin(adder_28_cout), .cout(adder_29_cout));
  Adder #(.width(64)) adder_30 (
    .a(adder_29_out), .b(and_33_out), .out(adder_30_out), .cin(adder_29_cout), .cout(adder_30_cout));
  Adder #(.width(64)) adder_31 (
    .a(adder_30_out), .b(and_34_out), .out(adder_31_out), .cin(adder_30_cout), .cout(adder_31_cout));
  Adder #(.width(64)) adder_32 (
    .a(adder_31_out), .b(and_35_out), .out(adder_32_out), .cin(adder_31_cout), .cout(adder_32_cout));
  Adder #(.width(64)) adder_33 (
    .a(adder_32_out), .b(and_36_out), .out(adder_33_out), .cin(adder_32_cout));  // open: cout
  assign not_3_out = ~adder_33_out;  // NOT_Gate not_3, 64 bits wide
  Adder #(.width(64)) adder_34 (.a(not_3_out), .b(64'h1), .out(adder_34_out));  // open: cin, cout
  Multiplexer #(.width(64)) multiplexer_3 (
    .in0(adder_33_out), .in1(adder_34_out), .out({carry, result}), .sel(xor_1_out));
endmodule

module ALU_RV32I (
  input  [4:0] Operatsioon,
  input  [31:0] A,
  input  [31:0] B,
  output [31:0] Tulemus
);

  wire adder_1_cout, comparator_1_lt, decoder_1_out1, decoder_1_out2, decoder_1_out22, decoder_1_out23,
       not_1_out, or_1_out;
  wire [31:0] adder_1_out, and_1_out, bit_extender_1_out, bit_extender_2_out, bit_extender_3_out, or_2_out,
       shifter_1_out, shifter_2_out, shifter_3_out, xor_1_out, xor_2_out;

  Decoder #(.enable("false"), .select(5)) decoder_1 (
    .out1(decoder_1_out1), .out2(decoder_1_out2), .out22(decoder_1_out22), .out23(decoder_1_out23),
    .sel(Operatsioon));  // open: out0, out3, out4, out5, out6, out7, out8, out9, out10, out11, out12, out13, out14, out15, out16, out17, out18, out19, out20, out21, out24, out25, out26, out27, out28, out29, out30, out31
  or or_1 (or_1_out, decoder_1_out1, decoder_1_out2);
  assign bit_extender_1_out = {{31{or_1_out}}, or_1_out};  // Bit_Extender bit_extender_1
  assign xor_1_out = bit_extender_1_out ^ B;  // XOR_Gate xor_1, 32 bits wide
  Adder #(.width(32)) adder_1 (.a(A), .b(xor_1_out), .out(adder_1_out), .cin(or_1_out), .cout(adder_1_cout));
  not not_1 (not_1_out, adder_1_cout);
  Shifter #(.width(32)) shifter_1 (.in(A), .\dist (B[4:0]), .out(shifter_1_out));
  Shifter #(.shift("lr"), .width(32)) shifter_2 (.in(A), .\dist (B[4:0]), .out(shifter_2_out));
  Shifter #(.shift("ar"), .width(32)) shifter_3 (.in(A), .\dist (B[4:0]), .out(shifter_3_out));
  assign and_1_out = A & B;  // AND_Gate and_1, 32 bits wide
  assign or_2_out = A | B;  // OR_Gate or_2, 32 bits wide
  assign xor_2_out = A ^ B;  // XOR_Gate xor_2, 32 bits wide
  Comparator #(.width(32)) comparator_1 (.a(A), .b(B), .lt(comparator_1_lt));  // open: gt, eq
  assign bit_extender_2_out = {{31{1'b0}}, not_1_out};  // Bit_Extender bit_extender_2
  // Probe on shifter_1_out
  assign bit_extender_3_out = {{31{1'b0}}, comparator_1_lt};  // Bit_Extender bit_extender_3
  // Probe on Operatsioon
  Multiplexer #(.select(5), .width(32)) multiplexer_1 (
    .in0(adder_1_out), .in1(adder_1_out), .in2(bit_extender_2_out), .in3(shifter_1_out), .in4(shifter_2_out),
    .in5(shifter_3_out), .in6(and_1_out), .in7(or_2_out), .in8(xor_2_out), .in9(bit_extender_3_out),
    .in10({32{1'b0}}), .in11({32{1'b0}}), .in12({32{1'b0}}), .in13({32{1'b0}}), .in14({32{1'b0}}),
    .in15({32{1'b0}}), .in16({32{1'b0}}), .in17({32{1'b0}}), .in18({32{1'b0}}), .in19({32{1'b0}}),
    .in20({32{1'b0}}), .in21({32{1'b0}}), .in22({32{1'b0}}), .in23({32{1'b0}}), .in24({32{1'b0}}),
    .in25({32{1'b0}}), .in26({32{1'b0}}), .in27({32{1'b0}}), .in28({32{1'b0}}), .in29({32{1'b0}}),
    .in30({32{1'b0}}), .in31({32{1'b0}}), .out(Tulemus), .sel(Operatsioon));
endmodule

module Mstatus_register (
  input  [31:0] Andmed_sisse,
  input  Luba_kirjutamine,
  input  Loksu_sisenemine,
  input  Loksust_valjumine,
  input  Reset,
  input  Kell,
  output [31:0] Andmed_valja,
  output mie
);

  wire and_1_out, and_2_out, multiplexer_1_out, multiplexer_2_out, multiplexer_3_out, or_1_out, or_2_out;

  Multiplexer multiplexer_1 (
    .in0(Andmed_sisse[3]), .in1(Andmed_valja[7]), .out(multiplexer_1_out), .sel(Loksust_valjumine));
  Multiplexer multiplexer_2 (.in0(multiplexer_1_out), .in1(1'b0), .out(multiplexer_2_out), .sel(Loksu_sisenemine));
  Multiplexer multiplexer_3 (
    .in0(Andmed_sisse[7]), .in1(Andmed_valja[3]), .out(multiplexer_3_out), .sel(Loksu_sisenemine));
  or or_1 (or_1_out, Luba_kirjutamine, Loksu_sisenemine, Loksust_valjumine);
  or or_2 (or_2_out, Luba_kirjutamine, Loksu_sisenemine);
  and and_1 (and_1_out, or_2_out, Kell);
  D_Flip_Flop mie_ff (.D(multiplexer_2_out), .clk(and_2_out), .Q(Andmed_valja[3]), .reset(Reset));  // open: Qn, preset
  and and_2 (and_2_out, or_1_out, Kell);
  D_Flip_Flop mpie_ff (.D(multiplexer_3_out), .clk(and_1_out), .Q(Andmed_valja[7]), .reset(Reset));  // open: Qn, preset

  assign {Andmed_valja[31:8], Andmed_valja[6:4], Andmed_valja[2:0]} = 30'h600;
  assign mie = Andmed_valja[3];
endmodule
